// Logisim project B1_Group4.circ as structural Verilog: 2 circuits, main circuit main
// ALU
module main (
  input  cs0,
  input  cs1,
  input  cs2,
  input  A1,
  input  A2,
  input  A3,
  input  A4,
  input  B1,
  input  B2,
  input  B3,
  input  B4,
  output V,
  output Z,
  output S,
  output C,
  output F4,
  output F3,
  output F2,
  output F1
);

  wire Adder__2__s3, Adder__6__s2, Adder__9__s1, Adder__14__cout, Adder__15__s4, AND_k__3__1y, AND_k__6__2y,
       AND_k__8__3y, Mux1__4__y1, Mux1__7__y2, Mux1__9__y3, Mux1__12__y4, Mux2__4__y1, Mux2__7__y2,
       Mux2__9__y3, Mux2__12__y4, OR1__3__1y, OR1__6__2y, OR1__8__3y, OR1__11__4y, OR_k__3__1y, OR_k__6__2y,
       OR_k__8__3y, OR_k__11__4y, Xor_1__3__1y, Xor_1__6__2y, Xor_1__8__3y, Xor_1__11__4y, Xor_2__3__1y,
       Xor_2__8__3y, Xor_3__6__2y, Xor_3__8__3y, Xor_3__11__4y, xor_B__3__1y, xor_B__6__2y, xor_B__8__3y,
       xor_B__11__4y;

  _7486 Xor_2 (
    ._1__1A(cs1), ._2__1B(1'b1), ._3__1Y(Xor_2__3__1y), ._7__GND(1'b0), ._14__Vcc(1'b1), ._13__4B(1'b0),
    ._12__4A(Adder__14__cout), ._11__4Y(C), ._10__3B(A4), ._9__3A(Mux2__12__y4), ._8__3Y(Xor_2__8__3y));  // open: _4__2A, _5__2B, _6__2Y
  _7408 AND_k (
    ._1__1A(Xor_2__3__1y), ._2__1B(OR_k__3__1y), ._3__1Y(AND_k__3__1y), ._4__2A(cs2), ._5__2B(Xor_2__3__1y),
    ._6__2Y(AND_k__6__2y), ._7__GND(1'b0), ._14__Vcc(1'b1), ._13__4B(Xor_3__11__4y), ._12__4A(Xor_3__8__3y),
    ._11__4Y(V), ._10__3B(cs0), ._9__3A(cs1), ._8__3Y(AND_k__8__3y));
  _7432 OR1 (
    ._1__1A(A1), ._2__1B(B1), ._3__1Y(OR1__3__1y), ._4__2A(A2), ._5__2B(B2), ._6__2Y(OR1__6__2y),
    ._7__GND(1'b0), ._14__Vcc(1'b1), ._13__4B(B4), ._12__4A(A4), ._11__4Y(OR1__11__4y), ._10__3B(B3),
    ._9__3A(A3), ._8__3Y(OR1__8__3y));
  _7486 Xor_1 (
    ._1__1A(A1), ._2__1B(B1), ._3__1Y(Xor_1__3__1y), ._4__2A(A2), ._5__2B(B2), ._6__2Y(Xor_1__6__2y),
    ._7__GND(1'b0), ._14__Vcc(1'b1), ._13__4B(A4), ._12__4A(B4), ._11__4Y(Xor_1__11__4y), ._10__3B(A3),
    ._9__3A(B3), ._8__3Y(Xor_1__8__3y));
  _7432 OR_k (
    ._1__1A(cs2), ._2__1B(cs0), ._3__1Y(OR_k__3__1y), ._4__2A(F1), ._5__2B(OR_k__8__3y),
    ._6__2Y(OR_k__6__2y), ._7__GND(1'b0), ._14__Vcc(1'b1), ._13__4B(F4), ._12__4A(F3),
    ._11__4Y(OR_k__11__4y), ._10__3B(OR_k__11__4y), ._9__3A(F2), ._8__3Y(OR_k__8__3y));
  _74157 Mux1 (
    ._1__S(cs2), ._2__A1(OR1__3__1y), ._3__B1(Xor_1__3__1y), ._4__Y1(Mux1__4__y1), ._5__A2(OR1__6__2y),
    ._6__B2(Xor_1__6__2y), ._7__Y2(Mux1__7__y2), ._8__GND(1'b0), ._16__Vcc(1'b1), ._15__G(1'b0),
    ._14__A4(OR1__11__4y), ._13__B4(Xor_1__11__4y), ._12__Y4(Mux1__12__y4), ._11__A3(OR1__8__3y),
    ._10__B3(Xor_1__8__3y), ._9__Y3(Mux1__9__y3));
  _7486 xor_B (
    ._1__1A(cs1), ._2__1B(B1), ._3__1Y(xor_B__3__1y), ._4__2A(cs1), ._5__2B(B2), ._6__2Y(xor_B__6__2y),
    ._7__GND(1'b0), ._14__Vcc(1'b1), ._13__4B(B4), ._12__4A(cs1), ._11__4Y(xor_B__11__4y), ._10__3B(B3),
    ._9__3A(cs1), ._8__3Y(xor_B__8__3y));
  _7486 Xor_3 (
    ._1__1A(OR_k__6__2y), ._2__1B(1'b1), ._3__1Y(Z), ._4__2A(Xor_2__8__3y), ._5__2B(Adder__14__cout),
    ._6__2Y(Xor_3__6__2y), ._7__GND(1'b0), ._14__Vcc(1'b1), ._13__4B(1'b1), ._12__4A(AND_k__8__3y),
    ._11__4Y(Xor_3__11__4y), ._10__3B(F4), ._9__3A(Xor_3__6__2y), ._8__3Y(Xor_3__8__3y));
  _74157 Mux3 (
    ._1__S(AND_k__8__3y), ._2__A1(Adder__9__s1), ._3__B1(Mux1__4__y1), ._4__Y1(F1), ._5__A2(Adder__6__s2),
    ._6__B2(Mux1__7__y2), ._7__Y2(F2), ._8__GND(1'b0), ._16__Vcc(1'b1), ._15__G(1'b0),
    ._14__A4(Adder__15__s4), ._13__B4(Mux1__12__y4), ._12__Y4(F4), ._11__A3(Adder__2__s3),
    ._10__B3(Mux1__9__y3), ._9__Y3(F3));
  _74157 Mux2 (
    ._1__S(AND_k__3__1y), ._2__A1(xor_B__3__1y), ._3__B1(1'b0), ._4__Y1(Mux2__4__y1), ._5__A2(xor_B__6__2y),
    ._6__B2(1'b0), ._7__Y2(Mux2__7__y2), ._8__GND(1'b0), ._16__Vcc(1'b1), ._15__G(1'b0),
    ._14__A4(xor_B__11__4y), ._13__B4(1'b0), ._12__Y4(Mux2__12__y4), ._11__A3(xor_B__8__3y), ._10__B3(1'b0),
    ._9__Y3(Mux2__9__y3));
  _7483 Adder (
    ._1__A4(A4), ._2__S3(Adder__2__s3), ._3__A3(A3), ._4__B3(Mux2__9__y3), ._5__Vcc(Xor_3__11__4y),
    ._6__S2(Adder__6__s2), ._7__B2(Mux2__7__y2), ._8__A2(A2), ._16__B4(Mux2__12__y4),
    ._15__S4(Adder__15__s4), ._14__Cout(Adder__14__cout), ._13__Cin(AND_k__6__2y), ._12__GND(1'b0),
    ._11__B1(Mux2__4__y1), ._10__A1(A1), ._9__S1(Adder__9__s1));

  assign S = F4;

  // Notes on the sheet:
  //   CSE306 Assignment 1
  //   4 bit Arithmetic and Logic Unit
  //   Section : B1
  //   Participating rolls:
  //   1905065
  //   1905067
  //   1905069
  //   Control Signals
  //   cs2 cs1 cs0
  //   0     0     0
  //   0     0     1
  //   0     1     0
  //   0     1     1
  //   1     0     0
  //   1     0     1
  //   1     1     0
  //   1     1     1
  //   Group: 4
  //   1905076
  //   1905077
  //   Operation
  //   Add
  //   Transfer A
  //   Sub with Borrow
  //   OR
  //   Increment A
  //   Increment A
  //   Sub with Borrow
  //   XOR
  //   Functions for
  //   Symbol
  //   A+B
  //   A
  //   A+B'
  //   A|B
  //   A+1
  //   A+1
  //   A+B'
  //   A^B
endmodule

module two (
  input  in_1,
  input  in_2,
  input  in_3,
  input  in_4,
  output out_5
);

  wire undriven, undriven_2;

  _74157 u_74157_1 (
    ._1__S(in_1), ._2__A1(in_3), ._3__B1(in_4), ._4__Y1(out_5), ._15__G(in_2));  // open: _5__A2, _6__B2, _7__Y2, _8__GND, _16__Vcc, _14__A4, _13__B4, _12__Y4, _11__A3, _10__B3, _9__Y3
  main main_1 (
    .cs0(undriven), .cs1(undriven_2));  // open: cs2, A1, A2, A3, A4, B1, B2, B3, B4, V, Z, S, C, F4, F3, F2, F1
endmodule
