// Logisim project B1_Group4_FPA.circ as structural Verilog: 5 circuits, main circuit main
module main (
  input  [31:0] in_1,
  input  [31:0] in_2,
  output [31:0] out_3,
  output Underflow,
  output Overflow
);

  FloatingPointAdder floatingpointadder_1 (.A(in_1), .B(in_2), .F(out_3), .Underflow(Underflow), .Overflow(Overflow));

  // Notes on the sheet:
  //   CSE306 Assignment 2
  //   32 bit Floating Point Adder
  //   Section : B1
  //   Participating rolls:
  //   1905065
  //   1905067
  //   1905069
  //   Sign
  //   1bit
  //   Group: 4
  //   1905076
  //   1905077
  //   Exponent
  //   12bit
  //   Fraction
  //   19bit
endmodule

// FPA
module FloatingPointAdder (
  input  [31:0] A,
  input  [31:0] B,
  output [31:0] F,
  output Underflow,
  output Overflow
);

  wire and1bit2x1_1_out_2, and1bit2x1_2_out_2, control_1_c, inputsplitter_1_s1, inputsplitter_2_s1,
       mux1bit2x1_1_dataout, mux1bit2x1_2_dataout, not1bit_1_a_prime, or1bit12x1_1_out_2;
  wire [1:0] not1bit_2_a_prime, not1bit_3_a_prime, xor1bit2x1_1_dataout;
  wire [11:0] control_1_se, incrementexponent_1_a_1, inputsplitter_1_e12, inputsplitter_2_e12,
       inputsplitter_3_e12, mux12bit2x1_1_dataout, mux12bit2x1_2_dataout, normalizer_1_eout,
       rounder_1_e_rounded;
  wire [18:0] inputsplitter_1_f19, inputsplitter_2_f19, mux19bit2x1_1_dataout, mux19bit2x1_2_dataout,
       rounder_1_f_rounded;
  wire [31:0] adder32bit_1_dataout, customrightshifter_1_data_out, makesignificand_1_out32,
       makesignificand_2_out32, mux32bit2x1_1_dataout, normalizer_1_fout, outputsplitter_1__32,
       selectinverse_1_dataout, zero32bit_1_out_1;

  inputSplitter inputsplitter_1 (
    ._32(A), .s1(inputsplitter_1_s1), .e12(inputsplitter_1_e12), .f19(inputsplitter_1_f19));
  inputSplitter inputsplitter_2 (
    ._32(B), .s1(inputsplitter_2_s1), .e12(inputsplitter_2_e12), .f19(inputsplitter_2_f19));
  MUX1bit2x1 mux1bit2x1_1 (
    .S(control_1_c), .Data0(inputsplitter_1_s1), .Data1(inputsplitter_2_s1), .DataOut(mux1bit2x1_1_dataout));
  MUX1bit2x1 mux1bit2x1_2 (
    .S(not1bit_1_a_prime), .Data0(inputsplitter_1_s1), .Data1(inputsplitter_2_s1),
    .DataOut(mux1bit2x1_2_dataout));
  MUX12bit2x1 mux12bit2x1_1 (
    .S(control_1_c), .Data0(inputsplitter_1_e12), .Data1(inputsplitter_2_e12), .DataOut(mux12bit2x1_1_dataout));
  MUX19bit2x1 mux19bit2x1_1 (
    .S(control_1_c), .Data0(inputsplitter_1_f19), .Data1(inputsplitter_2_f19), .DataOut(mux19bit2x1_1_dataout));
  MUX19bit2x1 mux19bit2x1_2 (
    .S(not1bit_1_a_prime), .Data0(inputsplitter_1_f19), .Data1(inputsplitter_2_f19),
    .DataOut(mux19bit2x1_2_dataout));
  NOT1bit not1bit_1 (.A(control_1_c), .A_prime(not1bit_1_a_prime));
  Control control_1 (
    .Ae(inputsplitter_1_e12), .Be(inputsplitter_2_e12), .Af(inputsplitter_1_f19), .Bf(inputsplitter_2_f19),
    .Se(control_1_se), .C(control_1_c), .out_8(xor1bit2x1_1_dataout[1]));  // open: Sf
  incrementExponent incrementexponent_1 (.A(mux12bit2x1_1_dataout), .A_1(incrementexponent_1_a_1));  // open: Overflow
  makeSignificand makesignificand_1 (.in19(mux19bit2x1_1_dataout), .out32(makesignificand_1_out32));
  makeSignificand makesignificand_2 (.in19(mux19bit2x1_2_dataout), .out32(makesignificand_2_out32));
  XOR1bit2x1 xor1bit2x1_1 (
    .Data0(mux1bit2x1_1_dataout), .Data1(mux1bit2x1_2_dataout), .DataOut(xor1bit2x1_1_dataout[0]));
  NOT1bit not1bit_2 (.A(xor1bit2x1_1_dataout[0]), .A_prime(not1bit_2_a_prime[0]));
  CustomRightShifter customrightshifter_1 (
    .Shift_bit(1'b0), .Data_in(makesignificand_2_out32), .Shift_amount(control_1_se),
    .Data_out(customrightshifter_1_data_out));
  selectInverse selectinverse_1 (
    .Data_in(customrightshifter_1_data_out), .Selector(xor1bit2x1_1_dataout[0]),
    .DataOut(selectinverse_1_dataout));
  AND1bit2x1 and1bit2x1_1 (.in_1(not1bit_2_a_prime), .out_2(and1bit2x1_1_out_2));
  Adder32bit adder32bit_1 (
    .Data0(makesignificand_1_out32), .Data1(selectinverse_1_dataout), .Cin(xor1bit2x1_1_dataout[0]),
    .Cout(not1bit_2_a_prime[1]), .DataOut(adder32bit_1_dataout));
  AND1bit2x1 and1bit2x1_2 (.in_1(xor1bit2x1_1_dataout), .out_2(and1bit2x1_2_out_2));
  MUX12bit2x1 mux12bit2x1_2 (
    .S(and1bit2x1_1_out_2), .Data0(normalizer_1_eout), .Data1(incrementexponent_1_a_1),
    .DataOut(mux12bit2x1_2_dataout));
  Normalizer normalizer_1 (
    .Fin(adder32bit_1_dataout), .Ein(incrementexponent_1_a_1), .Fout(normalizer_1_fout),
    .Eout(normalizer_1_eout), .Underflow(not1bit_3_a_prime[1]));
  MUX32bit2x1 mux32bit2x1_1 (
    .S(and1bit2x1_1_out_2), .Data0(normalizer_1_fout), .Data1(adder32bit_1_dataout),
    .DataOut(mux32bit2x1_1_dataout));
  inputSplitter inputsplitter_3 (._32(F), .e12(inputsplitter_3_e12));  // open: s1, f19
  Rounder rounder_1 (
    .E_unrounded(mux12bit2x1_2_dataout), .F_unrounded(mux32bit2x1_1_dataout),
    .E_rounded(rounder_1_e_rounded), .F_rounded(rounder_1_f_rounded));
  OR1bit12x1 or1bit12x1_1 (.in_1(inputsplitter_3_e12), .out_2(or1bit12x1_1_out_2));
  outputSplitter outputsplitter_1 (
    ._1(mux1bit2x1_1_dataout), ._12(rounder_1_e_rounded), ._19(rounder_1_f_rounded),
    ._32(outputsplitter_1__32));
  MUX32bit2x1 mux32bit2x1_2 (
    .S(and1bit2x1_2_out_2), .Data0(outputsplitter_1__32), .Data1(zero32bit_1_out_1), .DataOut(F));
  Zero32bit zero32bit_1 (.out_1(zero32bit_1_out_1));
  NOT1bit not1bit_3 (.A(or1bit12x1_1_out_2), .A_prime(not1bit_3_a_prime[0]));
  OR1bit2x1 or1bit2x1_1 (.in_1(not1bit_3_a_prime), .out_2(Underflow));
  incrementExponent incrementexponent_2 (.A(rounder_1_e_rounded), .Overflow(Overflow));  // open: A_1
endmodule

module Control (
  input  [11:0] Ae,
  input  [11:0] Be,
  input  [18:0] Af,
  input  [18:0] Bf,
  output [11:0] Se,
  output [18:0] Sf,
  output C,
  output out_8
);

  wire adder12bit_1_cout, adder19bit_1_cout, or1bit12x1_1_out_2, or1bit19x1_1_out_2;
  wire [0:0] and1bit2x1_1_out_2, not1bit_3_a_prime;
  wire [1:1] not1bit_4_a_prime;
  wire [11:0] adder12bit_1_dataout, not12bit_1_dataout, xor12bit2x1_1_dataout;
  wire [11:11] not1bit_1_a_prime;
  wire [18:0] adder19bit_1_dataout, not19bit_1_dataout, xor19bit2x1_1_dataout;
  wire [18:18] not1bit_2_a_prime;

  NOT12bit not12bit_1 (.Data0(Be), .DataOut(not12bit_1_dataout));
  NOT19bit not19bit_1 (.Data0(Bf), .DataOut(not19bit_1_dataout));
  Adder12bit adder12bit_1 (
    .Data0(Ae), .Data1(not12bit_1_dataout), .Cin(1'b1), .Cout(adder12bit_1_cout),
    .DataOut(adder12bit_1_dataout));
  NOT1bit not1bit_1 (.A(adder12bit_1_cout), .A_prime(not1bit_1_a_prime[11]));
  Adder19bit adder19bit_1 (
    .Data0(Af), .Data1(not19bit_1_dataout), .Cin(1'b1), .Cout(adder19bit_1_cout),
    .DataOut(adder19bit_1_dataout));
  NOT1bit not1bit_2 (.A(adder19bit_1_cout), .A_prime(not1bit_2_a_prime[18]));
  XOR12bit2x1 xor12bit2x1_1 (
    .Data0(adder12bit_1_dataout), .Data1({12{not1bit_1_a_prime[11]}}), .DataOut(xor12bit2x1_1_dataout));
  Adder12bit adder12bit_2 (
    .Data0(xor12bit2x1_1_dataout), .Data1({12{1'b0}}), .Cin(not1bit_1_a_prime[11]), .DataOut(Se));  // open: Cout
  Adder19bit adder19bit_2 (
    .Data0(xor19bit2x1_1_dataout), .Data1({19{1'b0}}), .Cin(not1bit_2_a_prime[18]), .DataOut(Sf));  // open: Cout
  XOR19bit2x1 xor19bit2x1_1 (
    .Data0(adder19bit_1_dataout), .Data1({19{not1bit_2_a_prime[18]}}), .DataOut(xor19bit2x1_1_dataout));
  OR1bit12x1 or1bit12x1_1 (.in_1(Se), .out_2(or1bit12x1_1_out_2));
  OR1bit19x1 or1bit19x1_1 (.in_1(Sf), .out_2(or1bit19x1_1_out_2));
  NOT1bit not1bit_3 (.A(or1bit12x1_1_out_2), .A_prime(not1bit_3_a_prime[0]));
  NOT1bit not1bit_4 (.A(or1bit19x1_1_out_2), .A_prime(not1bit_4_a_prime[1]));
  AND1bit2x1 and1bit2x1_1 (.in_1({not1bit_2_a_prime[18], not1bit_3_a_prime[0]}), .out_2(and1bit2x1_1_out_2[0]));
  OR1bit2x1 or1bit2x1_1 (.in_1({not1bit_1_a_prime[11], and1bit2x1_1_out_2[0]}), .out_2(C));
  AND1bit2x1 and1bit2x1_2 (.in_1({not1bit_4_a_prime[1], not1bit_3_a_prime[0]}), .out_2(out_8));

  // Notes on the sheet:
  //   out_8: pull=down
endmodule

module Normalizer (
  input  [31:0] Fin,
  input  [11:0] Ein,
  output [31:0] Fout,
  output [11:0] Eout,
  output Underflow
);

  wire adder12bit_1_cout, or1bit12x1_1_out_2;
  wire [1:0] not1bit_1_a_prime;
  wire [11:0] not12bit_1_dataout, priorityencoder_1_out_2;

  PriorityEncoder priorityencoder_1 (.in_1(Fin), .out_2(priorityencoder_1_out_2));
  NOT12bit not12bit_1 (.Data0(priorityencoder_1_out_2), .DataOut(not12bit_1_dataout));
  Adder12bit adder12bit_1 (
    .Data0(not12bit_1_dataout), .Data1(Ein), .Cin(1'b1), .Cout(adder12bit_1_cout), .DataOut(Eout));
  OR1bit12x1 or1bit12x1_1 (.in_1(Eout), .out_2(or1bit12x1_1_out_2));
  CustomLeftShifter customleftshifter_1 (
    .Shift_bit(1'b0), .Data_in(Fin), .Shift_amount(priorityencoder_1_out_2), .Data_out(Fout));
  NOT1bit not1bit_1 (.A(adder12bit_1_cout), .A_prime(not1bit_1_a_prime[0]));
  NOT1bit not1bit_2 (.A(or1bit12x1_1_out_2), .A_prime(not1bit_1_a_prime[1]));
  OR1bit2x1 or1bit2x1_1 (.in_1(not1bit_1_a_prime), .out_2(Underflow));
endmodule

module Rounder (
  input  [11:0] E_unrounded,
  input  [31:0] F_unrounded,
  output [11:0] E_rounded,
  output [18:0] F_rounded
);

  wire adder19bit_1_cout, adder22bit_1_cout, adder25bit_1_cout, adder28bit_1_cout, adder31bit_1_cout,
       stickyadderbit_1_addbit, stickyadderbit_2_addbit, stickyadderbit_3_addbit, stickyadderbit_4_addbit,
       stickyadderbit_5_addbit;
  wire [3:0] mux22bit2x1_1_dataout;
  wire [11:0] adder12bit_1_dataout, adder12bit_2_dataout, adder12bit_3_dataout, adder12bit_4_dataout;
  wire [18:0] adder19bit_1_dataout;
  wire [18:1] mux22bit2x1_1_dataout_2;
  wire [21:0] adder22bit_1_dataout;
  wire [24:0] adder25bit_1_dataout, mux25bit2x1_1_dataout;
  wire [27:0] adder28bit_1_dataout, mux28bit2x1_1_dataout;
  wire [30:0] adder31bit_1_dataout, mux31bit2x1_1_dataout;

  StickyAdderBit stickyadderbit_1 (.LGRS({F_unrounded[1:0], 2'b00}), .addBit(stickyadderbit_1_addbit));
  Adder31bit adder31bit_1 (
    .Data0(F_unrounded[31:1]), .Data1({31{1'b0}}), .Cin(stickyadderbit_1_addbit), .Cout(adder31bit_1_cout),
    .DataOut(adder31bit_1_dataout));
  Adder12bit adder12bit_1 (
    .Data0(E_unrounded), .Data1({12{1'b0}}), .Cin(adder31bit_1_cout), .DataOut(adder12bit_1_dataout));  // open: Cout
  MUX31bit2x1 mux31bit2x1_1 (
    .S(adder31bit_1_cout), .Data0(adder31bit_1_dataout), .Data1({31{1'b0}}), .DataOut(mux31bit2x1_1_dataout));
  StickyAdderBit stickyadderbit_2 (.LGRS(mux31bit2x1_1_dataout[3:0]), .addBit(stickyadderbit_2_addbit));
  Adder28bit adder28bit_1 (
    .Data0(mux31bit2x1_1_dataout[30:3]), .Data1({28{1'b0}}), .Cin(stickyadderbit_2_addbit),
    .Cout(adder28bit_1_cout), .DataOut(adder28bit_1_dataout));
  Adder12bit adder12bit_2 (
    .Data0(adder12bit_1_dataout), .Data1({12{1'b0}}), .Cin(adder28bit_1_cout), .DataOut(adder12bit_2_dataout));  // open: Cout
  MUX28bit2x1 mux28bit2x1_1 (
    .S(adder28bit_1_cout), .Data0(adder28bit_1_dataout), .Data1({28{1'b0}}), .DataOut(mux28bit2x1_1_dataout));
  StickyAdderBit stickyadderbit_3 (.LGRS(mux28bit2x1_1_dataout[3:0]), .addBit(stickyadderbit_3_addbit));
  Adder25bit adder25bit_1 (
    .Data0(mux28bit2x1_1_dataout[27:3]), .Data1({25{1'b0}}), .Cin(stickyadderbit_3_addbit),
    .Cout(adder25bit_1_cout), .DataOut(adder25bit_1_dataout));
  Adder12bit adder12bit_3 (
    .Data0(adder12bit_2_dataout), .Data1({12{1'b0}}), .Cin(adder25bit_1_cout), .DataOut(adder12bit_3_dataout));  // open: Cout
  MUX25bit2x1 mux25bit2x1_1 (
    .S(adder25bit_1_cout), .Data0(adder25bit_1_dataout), .Data1({25{1'b0}}), .DataOut(mux25bit2x1_1_dataout));
  StickyAdderBit stickyadderbit_4 (.LGRS(mux25bit2x1_1_dataout[3:0]), .addBit(stickyadderbit_4_addbit));
  Adder22bit adder22bit_1 (
    .Data0(mux25bit2x1_1_dataout[24:3]), .Data1({22{1'b0}}), .Cin(stickyadderbit_4_addbit),
    .Cout(adder22bit_1_cout), .DataOut(adder22bit_1_dataout));
  Adder12bit adder12bit_4 (
    .Data0(adder12bit_3_dataout), .Data1({12{1'b0}}), .Cin(adder22bit_1_cout), .DataOut(adder12bit_4_dataout));  // open: Cout
  MUX22bit2x1 mux22bit2x1_1 (
    .S(adder22bit_1_cout), .Data0(adder22bit_1_dataout), .Data1({22{1'b0}}),
    .DataOut({mux22bit2x1_1_dataout_2, mux22bit2x1_1_dataout}));
  StickyAdderBit stickyadderbit_5 (.LGRS(mux22bit2x1_1_dataout), .addBit(stickyadderbit_5_addbit));
  Adder12bit adder12bit_5 (
    .Data0(adder12bit_4_dataout), .Data1({12{1'b0}}), .Cin(adder19bit_1_cout), .DataOut(E_rounded));  // open: Cout
  Adder19bit adder19bit_1 (
    .Data0({mux22bit2x1_1_dataout_2, mux22bit2x1_1_dataout[3]}), .Data1({19{1'b0}}),
    .Cin(stickyadderbit_5_addbit), .Cout(adder19bit_1_cout), .DataOut(adder19bit_1_dataout));
  MUX19bit2x1 mux19bit2x1_1 (
    .S(adder19bit_1_cout), .Data0(adder19bit_1_dataout), .Data1({19{1'b0}}), .DataOut(F_rounded));
endmodule
