// Logisim project Device.circ as structural Verilog
// AND2
module AND1bit2x1 (
  input  [1:0] in_1,
  output out_2
);

  _7408 u_7408_1 (
    ._1__1A(in_1[0]), ._2__1B(in_1[1]), ._3__1Y(out_2), ._7__GND(1'b0), ._14__Vcc(1'b1));  // open: _4__2A, _5__2B, _6__2Y, _13__4B, _12__4A, _11__4Y, _10__3B, _9__3A, _8__3Y
endmodule

// AND4
module AND1bit4x1 (
  input  [3:0] in_1,
  output out_2
);

  wire [1:0] and1bit2x1_1_out_2;

  AND1bit2x1 and1bit2x1_1 (.in_1(in_1[1:0]), .out_2(and1bit2x1_1_out_2[0]));
  AND1bit2x1 and1bit2x1_2 (.in_1(in_1[3:2]), .out_2(and1bit2x1_1_out_2[1]));
  AND1bit2x1 and1bit2x1_3 (.in_1(and1bit2x1_1_out_2), .out_2(out_2));
endmodule

// AND8
module AND1bit8x1 (
  input  [7:0] in_1,
  output out_2
);

  wire [1:0] and1bit4x1_1_out_2;

  AND1bit4x1 and1bit4x1_1 (.in_1(in_1[3:0]), .out_2(and1bit4x1_1_out_2[0]));
  AND1bit4x1 and1bit4x1_2 (.in_1(in_1[7:4]), .out_2(and1bit4x1_1_out_2[1]));
  AND1bit2x1 and1bit2x1_1 (.in_1(and1bit4x1_1_out_2), .out_2(out_2));
endmodule

// AND16
module AND1bit16x1 (
  input  [15:0] in_1,
  output out_2
);

  wire [1:0] and1bit8x1_1_out_2;

  AND1bit8x1 and1bit8x1_1 (.in_1(in_1[7:0]), .out_2(and1bit8x1_1_out_2[0]));
  AND1bit8x1 and1bit8x1_2 (.in_1(in_1[15:8]), .out_2(and1bit8x1_1_out_2[1]));
  AND1bit2x1 and1bit2x1_1 (.in_1(and1bit8x1_1_out_2), .out_2(out_2));
endmodule

// OR2
module OR1bit2x1 (
  input  [1:0] in_1,
  output out_2
);

  _7432 u_7432_1 (
    ._1__1A(in_1[0]), ._2__1B(in_1[1]), ._3__1Y(out_2), ._7__GND(1'b0), ._14__Vcc(1'b1));  // open: _4__2A, _5__2B, _6__2Y, _13__4B, _12__4A, _11__4Y, _10__3B, _9__3A, _8__3Y
endmodule

// OR4
module OR1bit4x1 (
  input  [3:0] in_1,
  output out_2
);

  wire [1:0] or1bit2x1_1_out_2;

  OR1bit2x1 or1bit2x1_1 (.in_1(in_1[1:0]), .out_2(or1bit2x1_1_out_2[0]));
  OR1bit2x1 or1bit2x1_2 (.in_1(in_1[3:2]), .out_2(or1bit2x1_1_out_2[1]));
  OR1bit2x1 or1bit2x1_3 (.in_1(or1bit2x1_1_out_2), .out_2(out_2));
endmodule

// OR8
module OR1bit8x1 (
  input  [7:0] in_1,
  output out_2
);

  wire [1:0] or1bit4x1_1_out_2;

  OR1bit4x1 or1bit4x1_1 (.in_1(in_1[3:0]), .out_2(or1bit4x1_1_out_2[0]));
  OR1bit4x1 or1bit4x1_2 (.in_1(in_1[7:4]), .out_2(or1bit4x1_1_out_2[1]));
  OR1bit2x1 or1bit2x1_1 (.in_1(or1bit4x1_1_out_2), .out_2(out_2));
endmodule

// OR12
module OR1bit12x1 (
  input  [11:0] in_1,
  output out_2
);

  wire [1:0] or1bit4x1_1_out_2;

  OR1bit4x1 or1bit4x1_1 (.in_1(in_1[3:0]), .out_2(or1bit4x1_1_out_2[0]));
  OR1bit8x1 or1bit8x1_1 (.in_1(in_1[11:4]), .out_2(or1bit4x1_1_out_2[1]));
  OR1bit2x1 or1bit2x1_1 (.in_1(or1bit4x1_1_out_2), .out_2(out_2));
endmodule

// OR16
module OR1bit16x1 (
  input  [15:0] in_1,
  output out_2
);

  wire [1:0] or1bit8x1_1_out_2;

  OR1bit8x1 or1bit8x1_1 (.in_1(in_1[7:0]), .out_2(or1bit8x1_1_out_2[0]));
  OR1bit8x1 or1bit8x1_2 (.in_1(in_1[15:8]), .out_2(or1bit8x1_1_out_2[1]));
  OR1bit2x1 or1bit2x1_1 (.in_1(or1bit8x1_1_out_2), .out_2(out_2));
endmodule

// OR19
module OR1bit19x1 (
  input  [18:0] in_1,
  output out_2
);

  wire [3:3] or1bit16x1_1_out_2;

  OR1bit16x1 or1bit16x1_1 (.in_1(in_1[18:3]), .out_2(or1bit16x1_1_out_2[3]));
  OR1bit4x1 or1bit4x1_1 (.in_1({or1bit16x1_1_out_2[3], in_1[2:0]}), .out_2(out_2));
endmodule

// M4
module MUX4bit2x1 (
  input  S,
  input  [3:0] Data0,
  input  [3:0] Data1,
  output [3:0] DataOut
);

  _74157 u_74157_1 (
    ._1__S(S), ._2__A1(Data0[0]), ._3__B1(Data1[0]), ._4__Y1(DataOut[0]), ._5__A2(Data0[1]),
    ._6__B2(Data1[1]), ._7__Y2(DataOut[1]), ._8__GND(1'b0), ._16__Vcc(1'b1), ._15__G(1'b0),
    ._14__A4(Data0[3]), ._13__B4(Data1[3]), ._12__Y4(DataOut[3]), ._11__A3(Data0[2]), ._10__B3(Data1[2]),
    ._9__Y3(DataOut[2]));
endmodule

// M3
module MUX3bit2x1 (
  input  S,
  input  [2:0] Data0,
  input  [2:0] Data1,
  output [2:0] DataOut
);

  wire n74157_1__12__y4, undriven, undriven_2;

  _74157 u_74157_1 (
    ._1__S(S), ._2__A1(Data0[0]), ._3__B1(Data1[0]), ._4__Y1(DataOut[0]), ._5__A2(Data0[1]),
    ._6__B2(Data1[1]), ._7__Y2(DataOut[1]), ._8__GND(1'b0), ._16__Vcc(1'b1), ._15__G(1'b0),
    ._14__A4(undriven), ._13__B4(undriven_2), ._12__Y4(n74157_1__12__y4), ._11__A3(Data0[2]),
    ._10__B3(Data1[2]), ._9__Y3(DataOut[2]));
endmodule

// M12
module MUX12bit2x1 (
  input  S,
  input  [11:0] Data0,
  input  [11:0] Data1,
  output [11:0] DataOut
);

  MUX4bit2x1 mux4bit2x1_1 (.S(S), .Data0(Data0[3:0]), .Data1(Data1[3:0]), .DataOut(DataOut[3:0]));
  MUX4bit2x1 mux4bit2x1_2 (.S(S), .Data0(Data0[7:4]), .Data1(Data1[7:4]), .DataOut(DataOut[7:4]));
  MUX4bit2x1 mux4bit2x1_3 (.S(S), .Data0(Data0[11:8]), .Data1(Data1[11:8]), .DataOut(DataOut[11:8]));
endmodule

// M19
module MUX19bit2x1 (
  input  S,
  input  [18:0] Data0,
  input  [18:0] Data1,
  output [18:0] DataOut
);

  MUX4bit2x1 mux4bit2x1_1 (.S(S), .Data0(Data0[3:0]), .Data1(Data1[3:0]), .DataOut(DataOut[3:0]));
  MUX4bit2x1 mux4bit2x1_2 (.S(S), .Data0(Data0[7:4]), .Data1(Data1[7:4]), .DataOut(DataOut[7:4]));
  MUX4bit2x1 mux4bit2x1_3 (.S(S), .Data0(Data0[11:8]), .Data1(Data1[11:8]), .DataOut(DataOut[11:8]));
  MUX4bit2x1 mux4bit2x1_4 (.S(S), .Data0(Data0[15:12]), .Data1(Data1[15:12]), .DataOut(DataOut[15:12]));
  MUX3bit2x1 mux3bit2x1_1 (.S(S), .Data0(Data0[18:16]), .Data1(Data1[18:16]), .DataOut(DataOut[18:16]));
endmodule

// M32
module MUX32bit2x1 (
  input  S,
  input  [31:0] Data0,
  input  [31:0] Data1,
  output [31:0] DataOut
);

  MUX4bit2x1 mux4bit2x1_1 (.S(S), .Data0(Data0[3:0]), .Data1(Data1[3:0]), .DataOut(DataOut[3:0]));
  MUX4bit2x1 mux4bit2x1_2 (.S(S), .Data0(Data0[7:4]), .Data1(Data1[7:4]), .DataOut(DataOut[7:4]));
  MUX4bit2x1 mux4bit2x1_3 (.S(S), .Data0(Data0[11:8]), .Data1(Data1[11:8]), .DataOut(DataOut[11:8]));
  MUX4bit2x1 mux4bit2x1_4 (.S(S), .Data0(Data0[15:12]), .Data1(Data1[15:12]), .DataOut(DataOut[15:12]));
  MUX4bit2x1 mux4bit2x1_5 (.S(S), .Data0(Data0[19:16]), .Data1(Data1[19:16]), .DataOut(DataOut[19:16]));
  MUX4bit2x1 mux4bit2x1_6 (.S(S), .Data0(Data0[23:20]), .Data1(Data1[23:20]), .DataOut(DataOut[23:20]));
  MUX4bit2x1 mux4bit2x1_7 (.S(S), .Data0(Data0[27:24]), .Data1(Data1[27:24]), .DataOut(DataOut[27:24]));
  MUX4bit2x1 mux4bit2x1_8 (.S(S), .Data0(Data0[31:28]), .Data1(Data1[31:28]), .DataOut(DataOut[31:28]));
endmodule

// M31
module MUX31bit2x1 (
  input  S,
  input  [30:0] Data0,
  input  [30:0] Data1,
  output [30:0] DataOut
);

  MUX4bit2x1 mux4bit2x1_1 (.S(S), .Data0(Data0[3:0]), .Data1(Data1[3:0]), .DataOut(DataOut[3:0]));
  MUX4bit2x1 mux4bit2x1_2 (.S(S), .Data0(Data0[7:4]), .Data1(Data1[7:4]), .DataOut(DataOut[7:4]));
  MUX4bit2x1 mux4bit2x1_3 (.S(S), .Data0(Data0[11:8]), .Data1(Data1[11:8]), .DataOut(DataOut[11:8]));
  MUX4bit2x1 mux4bit2x1_4 (.S(S), .Data0(Data0[15:12]), .Data1(Data1[15:12]), .DataOut(DataOut[15:12]));
  MUX4bit2x1 mux4bit2x1_5 (.S(S), .Data0(Data0[19:16]), .Data1(Data1[19:16]), .DataOut(DataOut[19:16]));
  MUX4bit2x1 mux4bit2x1_6 (.S(S), .Data0(Data0[23:20]), .Data1(Data1[23:20]), .DataOut(DataOut[23:20]));
  MUX4bit2x1 mux4bit2x1_7 (.S(S), .Data0(Data0[27:24]), .Data1(Data1[27:24]), .DataOut(DataOut[27:24]));
  MUX3bit2x1 mux3bit2x1_1 (.S(S), .Data0(Data0[30:28]), .Data1(Data1[30:28]), .DataOut(DataOut[30:28]));
endmodule

// M28
module MUX28bit2x1 (
  input  S,
  input  [27:0] Data0,
  input  [27:0] Data1,
  output [27:0] DataOut
);

  MUX4bit2x1 mux4bit2x1_1 (.S(S), .Data0(Data0[3:0]), .Data1(Data1[3:0]), .DataOut(DataOut[3:0]));
  MUX4bit2x1 mux4bit2x1_2 (.S(S), .Data0(Data0[7:4]), .Data1(Data1[7:4]), .DataOut(DataOut[7:4]));
  MUX4bit2x1 mux4bit2x1_3 (.S(S), .Data0(Data0[11:8]), .Data1(Data1[11:8]), .DataOut(DataOut[11:8]));
  MUX4bit2x1 mux4bit2x1_4 (.S(S), .Data0(Data0[15:12]), .Data1(Data1[15:12]), .DataOut(DataOut[15:12]));
  MUX4bit2x1 mux4bit2x1_5 (.S(S), .Data0(Data0[19:16]), .Data1(Data1[19:16]), .DataOut(DataOut[19:16]));
  MUX4bit2x1 mux4bit2x1_6 (.S(S), .Data0(Data0[23:20]), .Data1(Data1[23:20]), .DataOut(DataOut[23:20]));
  MUX4bit2x1 mux4bit2x1_7 (.S(S), .Data0(Data0[27:24]), .Data1(Data1[27:24]), .DataOut(DataOut[27:24]));
endmodule

// M25
module MUX25bit2x1 (
  input  S,
  input  [24:0] Data0,
  input  [24:0] Data1,
  output [24:0] DataOut
);

  MUX4bit2x1 mux4bit2x1_1 (.S(S), .Data0(Data0[3:0]), .Data1(Data1[3:0]), .DataOut(DataOut[3:0]));
  MUX4bit2x1 mux4bit2x1_2 (.S(S), .Data0(Data0[7:4]), .Data1(Data1[7:4]), .DataOut(DataOut[7:4]));
  MUX4bit2x1 mux4bit2x1_3 (.S(S), .Data0(Data0[11:8]), .Data1(Data1[11:8]), .DataOut(DataOut[11:8]));
  MUX4bit2x1 mux4bit2x1_4 (.S(S), .Data0(Data0[15:12]), .Data1(Data1[15:12]), .DataOut(DataOut[15:12]));
  MUX3bit2x1 mux3bit2x1_1 (.S(S), .Data0(Data0[18:16]), .Data1(Data1[18:16]), .DataOut(DataOut[18:16]));
  MUX3bit2x1 mux3bit2x1_2 (.S(S), .Data0(Data0[21:19]), .Data1(Data1[21:19]), .DataOut(DataOut[21:19]));
  MUX3bit2x1 mux3bit2x1_3 (.S(S), .Data0(Data0[24:22]), .Data1(Data1[24:22]), .DataOut(DataOut[24:22]));
endmodule

// M22
module MUX22bit2x1 (
  input  S,
  input  [21:0] Data0,
  input  [21:0] Data1,
  output [21:0] DataOut
);

  MUX4bit2x1 mux4bit2x1_1 (.S(S), .Data0(Data0[3:0]), .Data1(Data1[3:0]), .DataOut(DataOut[3:0]));
  MUX4bit2x1 mux4bit2x1_2 (.S(S), .Data0(Data0[7:4]), .Data1(Data1[7:4]), .DataOut(DataOut[7:4]));
  MUX4bit2x1 mux4bit2x1_3 (.S(S), .Data0(Data0[11:8]), .Data1(Data1[11:8]), .DataOut(DataOut[11:8]));
  MUX4bit2x1 mux4bit2x1_4 (.S(S), .Data0(Data0[15:12]), .Data1(Data1[15:12]), .DataOut(DataOut[15:12]));
  MUX3bit2x1 mux3bit2x1_1 (.S(S), .Data0(Data0[18:16]), .Data1(Data1[18:16]), .DataOut(DataOut[18:16]));
  MUX3bit2x1 mux3bit2x1_2 (.S(S), .Data0(Data0[21:19]), .Data1(Data1[21:19]), .DataOut(DataOut[21:19]));
endmodule

// A3
module Adder3bit (
  input  Cin,
  input  [2:0] Data0,
  input  [2:0] Data1,
  output [2:0] DataOut,
  output Cout
);

  _7483 u_7483_1 (
    ._1__A4(1'b0), ._2__S3(DataOut[2]), ._3__A3(Data0[2]), ._4__B3(Data1[2]), ._5__Vcc(1'b1),
    ._6__S2(DataOut[1]), ._7__B2(Data1[1]), ._8__A2(Data0[1]), ._16__B4(1'b0), ._15__S4(Cout),
    ._13__Cin(Cin), ._12__GND(1'b0), ._11__B1(Data1[0]), ._10__A1(Data0[0]), ._9__S1(DataOut[0]));  // open: _14__Cout
endmodule

// A4
module Adder4bit (
  input  Cin,
  input  [3:0] Data0,
  input  [3:0] Data1,
  output [3:0] DataOut,
  output Cout
);

  _7483 u_7483_1 (
    ._1__A4(Data0[3]), ._2__S3(DataOut[2]), ._3__A3(Data0[2]), ._4__B3(Data1[2]), ._5__Vcc(1'b1),
    ._6__S2(DataOut[1]), ._7__B2(Data1[1]), ._8__A2(Data0[1]), ._16__B4(Data1[3]), ._15__S4(DataOut[3]),
    ._14__Cout(Cout), ._13__Cin(Cin), ._12__GND(1'b0), ._11__B1(Data1[0]), ._10__A1(Data0[0]),
    ._9__S1(DataOut[0]));
endmodule

// A12
module Adder12bit (
  input  Cin,
  input  [11:0] Data0,
  input  [11:0] Data1,
  output [11:0] DataOut,
  output Cout
);

  wire adder4bit_1_cout, adder4bit_2_cout;

  Adder4bit adder4bit_1 (
    .Data0(Data0[3:0]), .Data1(Data1[3:0]), .Cin(Cin), .Cout(adder4bit_1_cout), .DataOut(DataOut[3:0]));
  Adder4bit adder4bit_2 (
    .Data0(Data0[7:4]), .Data1(Data1[7:4]), .Cin(adder4bit_1_cout), .Cout(adder4bit_2_cout),
    .DataOut(DataOut[7:4]));
  Adder4bit adder4bit_3 (
    .Data0(Data0[11:8]), .Data1(Data1[11:8]), .Cin(adder4bit_2_cout), .Cout(Cout), .DataOut(DataOut[11:8]));
endmodule

// A19
module Adder19bit (
  input  Cin,
  input  [18:0] Data0,
  input  [18:0] Data1,
  output Cout,
  output [18:0] DataOut
);

  wire adder4bit_1_cout, adder4bit_2_cout, adder4bit_3_cout, adder4bit_4_cout;

  Adder4bit adder4bit_1 (
    .Data0(Data0[3:0]), .Data1(Data1[3:0]), .Cin(Cin), .Cout(adder4bit_1_cout), .DataOut(DataOut[3:0]));
  Adder4bit adder4bit_2 (
    .Data0(Data0[7:4]), .Data1(Data1[7:4]), .Cin(adder4bit_1_cout), .Cout(adder4bit_2_cout),
    .DataOut(DataOut[7:4]));
  Adder4bit adder4bit_3 (
    .Data0(Data0[11:8]), .Data1(Data1[11:8]), .Cin(adder4bit_2_cout), .Cout(adder4bit_3_cout),
    .DataOut(DataOut[11:8]));
  Adder4bit adder4bit_4 (
    .Data0(Data0[15:12]), .Data1(Data1[15:12]), .Cin(adder4bit_3_cout), .Cout(adder4bit_4_cout),
    .DataOut(DataOut[15:12]));
  Adder3bit adder3bit_1 (
    .Data0(Data0[18:16]), .Data1(Data1[18:16]), .Cin(adder4bit_4_cout), .Cout(Cout), .DataOut(DataOut[18:16]));
endmodule

// A22
module Adder22bit (
  input  Cin,
  input  [21:0] Data0,
  input  [21:0] Data1,
  output Cout,
  output [21:0] DataOut
);

  wire adder3bit_1_cout, adder4bit_1_cout, adder4bit_2_cout, adder4bit_3_cout, adder4bit_4_cout;

  Adder4bit adder4bit_1 (
    .Data0(Data0[3:0]), .Data1(Data1[3:0]), .Cin(Cin), .Cout(adder4bit_1_cout), .DataOut(DataOut[3:0]));
  Adder4bit adder4bit_2 (
    .Data0(Data0[7:4]), .Data1(Data1[7:4]), .Cin(adder4bit_1_cout), .Cout(adder4bit_2_cout),
    .DataOut(DataOut[7:4]));
  Adder4bit adder4bit_3 (
    .Data0(Data0[11:8]), .Data1(Data1[11:8]), .Cin(adder4bit_2_cout), .Cout(adder4bit_3_cout),
    .DataOut(DataOut[11:8]));
  Adder4bit adder4bit_4 (
    .Data0(Data0[15:12]), .Data1(Data1[15:12]), .Cin(adder4bit_3_cout), .Cout(adder4bit_4_cout),
    .DataOut(DataOut[15:12]));
  Adder3bit adder3bit_1 (
    .Data0(Data0[18:16]), .Data1(Data1[18:16]), .Cin(adder4bit_4_cout), .Cout(adder3bit_1_cout),
    .DataOut(DataOut[18:16]));
  Adder3bit adder3bit_2 (
    .Data0(Data0[21:19]), .Data1(Data1[21:19]), .Cin(adder3bit_1_cout), .Cout(Cout), .DataOut(DataOut[21:19]));
endmodule

// A25
module Adder25bit (
  input  Cin,
  input  [24:0] Data0,
  input  [24:0] Data1,
  output Cout,
  output [24:0] DataOut
);

  wire adder3bit_1_cout, adder3bit_2_cout, adder4bit_1_cout, adder4bit_2_cout, adder4bit_3_cout,
       adder4bit_4_cout;

  Adder4bit adder4bit_1 (
    .Data0(Data0[3:0]), .Data1(Data1[3:0]), .Cin(Cin), .Cout(adder4bit_1_cout), .DataOut(DataOut[3:0]));
  Adder4bit adder4bit_2 (
    .Data0(Data0[7:4]), .Data1(Data1[7:4]), .Cin(adder4bit_1_cout), .Cout(adder4bit_2_cout),
    .DataOut(DataOut[7:4]));
  Adder4bit adder4bit_3 (
    .Data0(Data0[11:8]), .Data1(Data1[11:8]), .Cin(adder4bit_2_cout), .Cout(adder4bit_3_cout),
    .DataOut(DataOut[11:8]));
  Adder4bit adder4bit_4 (
    .Data0(Data0[15:12]), .Data1(Data1[15:12]), .Cin(adder4bit_3_cout), .Cout(adder4bit_4_cout),
    .DataOut(DataOut[15:12]));
  Adder3bit adder3bit_1 (
    .Data0(Data0[18:16]), .Data1(Data1[18:16]), .Cin(adder4bit_4_cout), .Cout(adder3bit_1_cout),
    .DataOut(DataOut[18:16]));
  Adder3bit adder3bit_2 (
    .Data0(Data0[21:19]), .Data1(Data1[21:19]), .Cin(adder3bit_1_cout), .Cout(adder3bit_2_cout),
    .DataOut(DataOut[21:19]));
  Adder3bit adder3bit_3 (
    .Data0(Data0[24:22]), .Data1(Data1[24:22]), .Cin(adder3bit_2_cout), .Cout(Cout), .DataOut(DataOut[24:22]));
endmodule

// A28
module Adder28bit (
  input  Cin,
  input  [27:0] Data0,
  input  [27:0] Data1,
  output Cout,
  output [27:0] DataOut
);

  wire adder4bit_1_cout, adder4bit_2_cout, adder4bit_3_cout, adder4bit_4_cout, adder4bit_5_cout,
       adder4bit_6_cout;

  Adder4bit adder4bit_1 (
    .Data0(Data0[3:0]), .Data1(Data1[3:0]), .Cin(Cin), .Cout(adder4bit_1_cout), .DataOut(DataOut[3:0]));
  Adder4bit adder4bit_2 (
    .Data0(Data0[7:4]), .Data1(Data1[7:4]), .Cin(adder4bit_1_cout), .Cout(adder4bit_2_cout),
    .DataOut(DataOut[7:4]));
  Adder4bit adder4bit_3 (
    .Data0(Data0[11:8]), .Data1(Data1[11:8]), .Cin(adder4bit_2_cout), .Cout(adder4bit_3_cout),
    .DataOut(DataOut[11:8]));
  Adder4bit adder4bit_4 (
    .Data0(Data0[15:12]), .Data1(Data1[15:12]), .Cin(adder4bit_3_cout), .Cout(adder4bit_4_cout),
    .DataOut(DataOut[15:12]));
  Adder4bit adder4bit_5 (
    .Data0(Data0[19:16]), .Data1(Data1[19:16]), .Cin(adder4bit_4_cout), .Cout(adder4bit_5_cout),
    .DataOut(DataOut[19:16]));
  Adder4bit adder4bit_6 (
    .Data0(Data0[23:20]), .Data1(Data1[23:20]), .Cin(adder4bit_5_cout), .Cout(adder4bit_6_cout),
    .DataOut(DataOut[23:20]));
  Adder4bit adder4bit_7 (
    .Data0(Data0[27:24]), .Data1(Data1[27:24]), .Cin(adder4bit_6_cout), .Cout(Cout), .DataOut(DataOut[27:24]));
endmodule

// A31
module Adder31bit (
  input  Cin,
  input  [30:0] Data0,
  input  [30:0] Data1,
  output [30:0] DataOut,
  output Cout
);

  wire adder4bit_1_cout, adder4bit_2_cout, adder4bit_3_cout, adder4bit_4_cout, adder4bit_5_cout,
       adder4bit_6_cout, adder4bit_7_cout;

  Adder4bit adder4bit_1 (
    .Data0(Data0[3:0]), .Data1(Data1[3:0]), .Cin(Cin), .Cout(adder4bit_1_cout), .DataOut(DataOut[3:0]));
  Adder4bit adder4bit_2 (
    .Data0(Data0[7:4]), .Data1(Data1[7:4]), .Cin(adder4bit_1_cout), .Cout(adder4bit_2_cout),
    .DataOut(DataOut[7:4]));
  Adder4bit adder4bit_3 (
    .Data0(Data0[11:8]), .Data1(Data1[11:8]), .Cin(adder4bit_2_cout), .Cout(adder4bit_3_cout),
    .DataOut(DataOut[11:8]));
  Adder4bit adder4bit_4 (
    .Data0(Data0[15:12]), .Data1(Data1[15:12]), .Cin(adder4bit_3_cout), .Cout(adder4bit_4_cout),
    .DataOut(DataOut[15:12]));
  Adder4bit adder4bit_5 (
    .Data0(Data0[19:16]), .Data1(Data1[19:16]), .Cin(adder4bit_4_cout), .Cout(adder4bit_5_cout),
    .DataOut(DataOut[19:16]));
  Adder4bit adder4bit_6 (
    .Data0(Data0[23:20]), .Data1(Data1[23:20]), .Cin(adder4bit_5_cout), .Cout(adder4bit_6_cout),
    .DataOut(DataOut[23:20]));
  Adder4bit adder4bit_7 (
    .Data0(Data0[27:24]), .Data1(Data1[27:24]), .Cin(adder4bit_6_cout), .Cout(adder4bit_7_cout),
    .DataOut(DataOut[27:24]));
  Adder3bit adder3bit_1 (
    .Data0(Data0[30:28]), .Data1(Data1[30:28]), .Cin(adder4bit_7_cout), .Cout(Cout), .DataOut(DataOut[30:28]));
endmodule

// A32
module Adder32bit (
  input  Cin,
  input  [31:0] Data0,
  input  [31:0] Data1,
  output [31:0] DataOut,
  output Cout
);

  wire adder4bit_1_cout, adder4bit_2_cout, adder4bit_3_cout, adder4bit_4_cout, adder4bit_5_cout,
       adder4bit_6_cout, adder4bit_7_cout;

  Adder4bit adder4bit_1 (
    .Data0(Data0[3:0]), .Data1(Data1[3:0]), .Cin(Cin), .Cout(adder4bit_1_cout), .DataOut(DataOut[3:0]));
  Adder4bit adder4bit_2 (
    .Data0(Data0[7:4]), .Data1(Data1[7:4]), .Cin(adder4bit_1_cout), .Cout(adder4bit_2_cout),
    .DataOut(DataOut[7:4]));
  Adder4bit adder4bit_3 (
    .Data0(Data0[11:8]), .Data1(Data1[11:8]), .Cin(adder4bit_2_cout), .Cout(adder4bit_3_cout),
    .DataOut(DataOut[11:8]));
  Adder4bit adder4bit_4 (
    .Data0(Data0[15:12]), .Data1(Data1[15:12]), .Cin(adder4bit_3_cout), .Cout(adder4bit_4_cout),
    .DataOut(DataOut[15:12]));
  Adder4bit adder4bit_5 (
    .Data0(Data0[19:16]), .Data1(Data1[19:16]), .Cin(adder4bit_4_cout), .Cout(adder4bit_5_cout),
    .DataOut(DataOut[19:16]));
  Adder4bit adder4bit_6 (
    .Data0(Data0[23:20]), .Data1(Data1[23:20]), .Cin(adder4bit_5_cout), .Cout(adder4bit_6_cout),
    .DataOut(DataOut[23:20]));
  Adder4bit adder4bit_7 (
    .Data0(Data0[27:24]), .Data1(Data1[27:24]), .Cin(adder4bit_6_cout), .Cout(adder4bit_7_cout),
    .DataOut(DataOut[27:24]));
  Adder4bit adder4bit_8 (
    .Data0(Data0[31:28]), .Data1(Data1[31:28]), .Cin(adder4bit_7_cout), .Cout(Cout), .DataOut(DataOut[31:28]));
endmodule

// XOR4
module XOR4bit2x1 (
  input  [3:0] Data0,
  input  [3:0] Data1,
  output [3:0] DataOut
);

  _7486 u_7486_1 (
    ._1__1A(Data0[0]), ._2__1B(Data1[0]), ._3__1Y(DataOut[0]), ._4__2A(Data0[1]), ._5__2B(Data1[1]),
    ._6__2Y(DataOut[1]), ._7__GND(1'b0), ._14__Vcc(1'b1), ._13__4B(Data0[3]), ._12__4A(Data1[3]),
    ._11__4Y(DataOut[3]), ._10__3B(Data0[2]), ._9__3A(Data1[2]), ._8__3Y(DataOut[2]));
endmodule

// XOR3
module XOR3bit2x1 (
  input  [2:0] Data0,
  input  [2:0] Data1,
  output [2:0] DataOut
);

  wire n7486_1__11__4y, undriven, undriven_2;

  _7486 u_7486_1 (
    ._1__1A(Data0[0]), ._2__1B(Data1[0]), ._3__1Y(DataOut[0]), ._4__2A(Data0[1]), ._5__2B(Data1[1]),
    ._6__2Y(DataOut[1]), ._7__GND(1'b0), ._14__Vcc(1'b1), ._13__4B(undriven), ._12__4A(undriven_2),
    ._11__4Y(n7486_1__11__4y), ._10__3B(Data0[2]), ._9__3A(Data1[2]), ._8__3Y(DataOut[2]));
endmodule

// XOR12
module XOR12bit2x1 (
  input  [11:0] Data0,
  input  [11:0] Data1,
  output [11:0] DataOut
);

  XOR4bit2x1 xor4bit2x1_1 (.Data0(Data0[3:0]), .Data1(Data1[3:0]), .DataOut(DataOut[3:0]));
  XOR4bit2x1 xor4bit2x1_2 (.Data0(Data0[7:4]), .Data1(Data1[7:4]), .DataOut(DataOut[7:4]));
  XOR4bit2x1 xor4bit2x1_3 (.Data0(Data0[11:8]), .Data1(Data1[11:8]), .DataOut(DataOut[11:8]));
endmodule

// XOR19
module XOR19bit2x1 (
  input  [18:0] Data0,
  input  [18:0] Data1,
  output [18:0] DataOut
);

  XOR4bit2x1 xor4bit2x1_1 (.Data0(Data0[3:0]), .Data1(Data1[3:0]), .DataOut(DataOut[3:0]));
  XOR4bit2x1 xor4bit2x1_2 (.Data0(Data0[7:4]), .Data1(Data1[7:4]), .DataOut(DataOut[7:4]));
  XOR4bit2x1 xor4bit2x1_3 (.Data0(Data0[11:8]), .Data1(Data1[11:8]), .DataOut(DataOut[11:8]));
  XOR4bit2x1 xor4bit2x1_4 (.Data0(Data0[15:12]), .Data1(Data1[15:12]), .DataOut(DataOut[15:12]));
  XOR3bit2x1 xor3bit2x1_1 (.Data0(Data0[18:16]), .Data1(Data1[18:16]), .DataOut(DataOut[18:16]));
endmodule

// XOR32
module XOR32bit2x1 (
  input  [31:0] Data0,
  input  [31:0] Data1,
  output [31:0] DataOut
);

  XOR4bit2x1 xor4bit2x1_1 (.Data0(Data0[3:0]), .Data1(Data1[3:0]), .DataOut(DataOut[3:0]));
  XOR4bit2x1 xor4bit2x1_2 (.Data0(Data0[7:4]), .Data1(Data1[7:4]), .DataOut(DataOut[7:4]));
  XOR4bit2x1 xor4bit2x1_3 (.Data0(Data0[11:8]), .Data1(Data1[11:8]), .DataOut(DataOut[11:8]));
  XOR4bit2x1 xor4bit2x1_4 (.Data0(Data0[15:12]), .Data1(Data1[15:12]), .DataOut(DataOut[15:12]));
  XOR4bit2x1 xor4bit2x1_5 (.Data0(Data0[19:16]), .Data1(Data1[19:16]), .DataOut(DataOut[19:16]));
  XOR4bit2x1 xor4bit2x1_6 (.Data0(Data0[23:20]), .Data1(Data1[23:20]), .DataOut(DataOut[23:20]));
  XOR4bit2x1 xor4bit2x1_7 (.Data0(Data0[27:24]), .Data1(Data1[27:24]), .DataOut(DataOut[27:24]));
  XOR4bit2x1 xor4bit2x1_8 (.Data0(Data0[31:28]), .Data1(Data1[31:28]), .DataOut(DataOut[31:28]));
endmodule

// NOT1
module NOT1bit (
  input  A,
  output A_prime
);

  _7404 u_7404_1 (
    ._1__1A(A), ._2__1Y(A_prime), ._7__GND(1'b0), ._14__Vcc(1'b1));  // open: _3__2A, _4__2Y, _5__3A, _6__3Y, _13__6A, _12__6Y, _11__5A, _10__5Y, _9__4A, _8__4Y
endmodule

// NOT3
module NOT3bit (
  input  [2:0] Data0,
  output [2:0] DataOut
);

  _7404 u_7404_1 (
    ._1__1A(Data0[0]), ._2__1Y(DataOut[0]), ._3__2A(Data0[1]), ._4__2Y(DataOut[1]), ._5__3A(Data0[2]),
    ._6__3Y(DataOut[2]), ._7__GND(1'b0), ._14__Vcc(1'b1));  // open: _13__6A, _12__6Y, _11__5A, _10__5Y, _9__4A, _8__4Y
endmodule

// NOT4
module NOT4bit (
  input  [3:0] Data0,
  output [3:0] DataOut
);

  _7404 u_7404_1 (
    ._1__1A(Data0[0]), ._2__1Y(DataOut[0]), ._3__2A(Data0[1]), ._4__2Y(DataOut[1]), ._5__3A(Data0[2]),
    ._6__3Y(DataOut[2]), ._7__GND(1'b0), ._14__Vcc(1'b1), ._13__6A(Data0[3]), ._12__6Y(DataOut[3]));  // open: _11__5A, _10__5Y, _9__4A, _8__4Y
endmodule

// NOT12
module NOT12bit (
  input  [11:0] Data0,
  output [11:0] DataOut
);

  NOT4bit not4bit_1 (.Data0(Data0[3:0]), .DataOut(DataOut[3:0]));
  NOT4bit not4bit_2 (.Data0(Data0[7:4]), .DataOut(DataOut[7:4]));
  NOT4bit not4bit_3 (.Data0(Data0[11:8]), .DataOut(DataOut[11:8]));
endmodule

// Comp4
module CompareWith4 (
  input  [2:0] in_1,
  output out_2,
  output out_3,
  output out_4
);

  wire [0:0] not1bit_1_a_prime, not1bit_2_a_prime;
  wire [1:0] adder3bit_2_cout;
  wire [2:0] not3bit_1_dataout, not3bit_2_dataout;

  NOT3bit not3bit_1 (.Data0(3'b100), .DataOut(not3bit_1_dataout));
  NOT3bit not3bit_2 (.Data0(in_1), .DataOut(not3bit_2_dataout));
  Adder3bit adder3bit_1 (
    .Data0(in_1), .Data1(not3bit_1_dataout), .Cin(1'b1), .Cout(adder3bit_2_cout[0]));  // open: DataOut
  Adder3bit adder3bit_2 (
    .Data0(3'b100), .Data1(not3bit_2_dataout), .Cin(1'b1), .Cout(adder3bit_2_cout[1]));  // open: DataOut
  NOT1bit not1bit_1 (.A(adder3bit_2_cout[0]), .A_prime(not1bit_1_a_prime[0]));
  NOT1bit not1bit_2 (.A(adder3bit_2_cout[1]), .A_prime(not1bit_2_a_prime[0]));
  AND1bit2x1 and1bit2x1_1 (.in_1({adder3bit_2_cout[1], not1bit_1_a_prime[0]}), .out_2(out_2));
  AND1bit2x1 and1bit2x1_2 (.in_1(adder3bit_2_cout), .out_2(out_3));
  AND1bit2x1 and1bit2x1_3 (.in_1({adder3bit_2_cout[0], not1bit_2_a_prime[0]}), .out_2(out_4));
endmodule

// GRS
module StickyAdderBit (
  input  [3:0] LGRS,
  output addBit
);

  wire [0:0] comparewith4_1_out_2, comparewith4_1_out_3, comparewith4_1_out_4;
  wire [1:0] and1bit2x1_1_out_2, or1bit2x1_1_out_2;

  CompareWith4 comparewith4_1 (
    .in_1(LGRS[2:0]), .out_2(comparewith4_1_out_2[0]), .out_3(comparewith4_1_out_3[0]),
    .out_4(comparewith4_1_out_4[0]));
  AND1bit2x1 and1bit2x1_1 (.in_1({1'b0, comparewith4_1_out_2[0]}), .out_2(and1bit2x1_1_out_2[0]));
  AND1bit2x1 and1bit2x1_2 (.in_1({LGRS[3], comparewith4_1_out_3[0]}), .out_2(and1bit2x1_1_out_2[1]));
  OR1bit2x1 or1bit2x1_1 (.in_1(and1bit2x1_1_out_2), .out_2(or1bit2x1_1_out_2[0]));
  AND1bit2x1 and1bit2x1_3 (.in_1({1'b1, comparewith4_1_out_4[0]}), .out_2(or1bit2x1_1_out_2[1]));
  OR1bit2x1 or1bit2x1_2 (.in_1(or1bit2x1_1_out_2), .out_2(addBit));
endmodule

// in
module inputSplitter (
  input  [31:0] _32,
  output s1,
  output [11:0] e12,
  output [18:0] f19
);


  assign e12 = _32[30:19];
  assign f19 = _32[18:0];
  assign s1 = _32[31];
endmodule

// out
module outputSplitter (
  input  _1,
  input  [11:0] _12,
  input  [18:0] _19,
  output [31:0] _32
);


  assign _32 = {_1, _12, _19};
endmodule

// 1
module makeSignificand (
  input  [18:0] in19,
  output [31:0] out32
);


  assign out32 = {1'b1, in19, {12{1'b0}}};
endmodule

// InvSel
module selectInverse (
  input  [31:0] Data_in,
  input  Selector,
  output [31:0] DataOut
);

  XOR32bit2x1 xor32bit2x1_1 (.Data0(Data_in), .Data1({32{Selector}}), .DataOut(DataOut));
endmodule

// incExp
module incrementExponent (
  input  [11:0] A,
  output [11:0] A_1,
  output Overflow
);

  Adder12bit adder12bit_1 (.Data0({12{1'b0}}), .Data1(A), .Cin(1'b1), .Cout(Overflow), .DataOut(A_1));
endmodule

// >>
module CustomRightShifter (
  input  Shift_bit,
  input  [31:0] Data_in,
  input  [11:0] Shift_amount,
  output [31:0] Data_out
);

  wire or1bit4x1_2_out_2;
  wire [0:0] mux32bit2x1_5_dataout, or1bit4x1_1_out_2;
  wire [1:0] mux32bit2x1_4_dataout;
  wire [3:0] mux32bit2x1_3_dataout;
  wire [7:0] mux32bit2x1_2_dataout;
  wire [15:0] mux32bit2x1_1_dataout, mux32bit2x1_1_dataout_2;
  wire [23:0] mux32bit2x1_2_dataout_2;
  wire [27:0] mux32bit2x1_3_dataout_2;
  wire [29:0] mux32bit2x1_4_dataout_2;
  wire [30:0] mux32bit2x1_5_dataout_2;

  OR1bit4x1 or1bit4x1_1 (
    .in_1({Shift_amount[8], Shift_amount[9], Shift_amount[10], Shift_amount[11]}),
    .out_2(or1bit4x1_1_out_2[0]));
  OR1bit4x1 or1bit4x1_2 (
    .in_1({Shift_amount[5], Shift_amount[6], Shift_amount[7], or1bit4x1_1_out_2[0]}),
    .out_2(or1bit4x1_2_out_2));
  MUX32bit2x1 mux32bit2x1_1 (
    .S(or1bit4x1_2_out_2), .Data0(Data_in), .Data1({32{1'b0}}),
    .DataOut({mux32bit2x1_1_dataout_2, mux32bit2x1_1_dataout}));
  MUX32bit2x1 mux32bit2x1_2 (
    .S(Shift_amount[4]), .Data0({mux32bit2x1_1_dataout_2, mux32bit2x1_1_dataout}),
    .Data1({{16{Shift_bit}}, mux32bit2x1_1_dataout_2}),
    .DataOut({mux32bit2x1_2_dataout_2, mux32bit2x1_2_dataout}));
  MUX32bit2x1 mux32bit2x1_3 (
    .S(Shift_amount[3]), .Data0({mux32bit2x1_2_dataout_2, mux32bit2x1_2_dataout}),
    .Data1({{8{Shift_bit}}, mux32bit2x1_2_dataout_2}),
    .DataOut({mux32bit2x1_3_dataout_2, mux32bit2x1_3_dataout}));
  MUX32bit2x1 mux32bit2x1_4 (
    .S(Shift_amount[2]), .Data0({mux32bit2x1_3_dataout_2, mux32bit2x1_3_dataout}),
    .Data1({{4{Shift_bit}}, mux32bit2x1_3_dataout_2}),
    .DataOut({mux32bit2x1_4_dataout_2, mux32bit2x1_4_dataout}));
  MUX32bit2x1 mux32bit2x1_5 (
    .S(Shift_amount[1]), .Data0({mux32bit2x1_4_dataout_2, mux32bit2x1_4_dataout}),
    .Data1({{2{Shift_bit}}, mux32bit2x1_4_dataout_2}),
    .DataOut({mux32bit2x1_5_dataout_2, mux32bit2x1_5_dataout[0]}));
  MUX32bit2x1 mux32bit2x1_6 (
    .S(Shift_amount[0]), .Data0({mux32bit2x1_5_dataout_2, mux32bit2x1_5_dataout[0]}),
    .Data1({Shift_bit, mux32bit2x1_5_dataout_2}), .DataOut(Data_out));
endmodule

// <<
module CustomLeftShifter (
  input  Shift_bit,
  input  [31:0] Data_in,
  input  [11:0] Shift_amount,
  output [31:0] Data_out
);

  wire or1bit4x1_2_out_2;
  wire [0:0] or1bit4x1_1_out_2;
  wire [31:0] mux32bit2x1_4_dataout;
  wire [31:1] mux32bit2x1_5_dataout;
  wire [31:4] mux32bit2x1_3_dataout;
  wire [31:8] mux32bit2x1_2_dataout;
  wire [31:16] mux32bit2x1_1_dataout, mux32bit2x1_1_dataout_2;
  wire [31:24] mux32bit2x1_2_dataout_2;
  wire [31:28] mux32bit2x1_3_dataout_2;
  wire [31:31] mux32bit2x1_5_dataout_2;

  OR1bit4x1 or1bit4x1_1 (
    .in_1({Shift_amount[8], Shift_amount[9], Shift_amount[10], Shift_amount[11]}),
    .out_2(or1bit4x1_1_out_2[0]));
  OR1bit4x1 or1bit4x1_2 (
    .in_1({Shift_amount[5], Shift_amount[6], Shift_amount[7], or1bit4x1_1_out_2[0]}),
    .out_2(or1bit4x1_2_out_2));
  MUX32bit2x1 mux32bit2x1_1 (
    .S(or1bit4x1_2_out_2), .Data0(Data_in), .Data1({32{1'b0}}),
    .DataOut({mux32bit2x1_1_dataout_2, mux32bit2x1_1_dataout}));
  MUX32bit2x1 mux32bit2x1_2 (
    .S(Shift_amount[4]), .Data0({mux32bit2x1_1_dataout_2, mux32bit2x1_1_dataout}),
    .Data1({mux32bit2x1_1_dataout, {16{Shift_bit}}}),
    .DataOut({mux32bit2x1_2_dataout_2, mux32bit2x1_2_dataout}));
  MUX32bit2x1 mux32bit2x1_3 (
    .S(Shift_amount[3]), .Data0({mux32bit2x1_2_dataout_2, mux32bit2x1_2_dataout}),
    .Data1({mux32bit2x1_2_dataout, {8{Shift_bit}}}),
    .DataOut({mux32bit2x1_3_dataout_2, mux32bit2x1_3_dataout}));
  MUX32bit2x1 mux32bit2x1_4 (
    .S(Shift_amount[2]), .Data0({mux32bit2x1_3_dataout_2, mux32bit2x1_3_dataout}),
    .Data1({mux32bit2x1_3_dataout, {4{Shift_bit}}}), .DataOut(mux32bit2x1_4_dataout));
  MUX32bit2x1 mux32bit2x1_5 (
    .S(Shift_amount[1]), .Data0(mux32bit2x1_4_dataout),
    .Data1({mux32bit2x1_4_dataout[29:0], {2{Shift_bit}}}),
    .DataOut({mux32bit2x1_5_dataout_2[31], mux32bit2x1_5_dataout}));
  MUX32bit2x1 mux32bit2x1_6 (
    .S(Shift_amount[0]), .Data0({mux32bit2x1_5_dataout_2[31], mux32bit2x1_5_dataout}),
    .Data1({mux32bit2x1_5_dataout, Shift_bit}), .DataOut(Data_out));
endmodule

// Prio
module PriorityEncoder (
  input  [31:0] in_1,
  output [11:0] out_2
);

  wire and1bit2x1_61_out_2;
  wire [0:0] not1bit_22_a_prime;
  wire [1:0] not1bit_1_a_prime, not1bit_3_a_prime, not1bit_4_a_prime, not1bit_5_a_prime, not1bit_6_a_prime,
       not1bit_7_a_prime, not1bit_8_a_prime, not1bit_9_a_prime, not1bit_10_a_prime, not1bit_11_a_prime,
       not1bit_12_a_prime, not1bit_13_a_prime, not1bit_14_a_prime, not1bit_15_a_prime, not1bit_16_a_prime,
       not1bit_17_a_prime, not1bit_18_a_prime, not1bit_19_a_prime, not1bit_20_a_prime, not1bit_21_a_prime,
       not1bit_23_a_prime, not1bit_24_a_prime, not1bit_25_a_prime, not1bit_26_a_prime, not1bit_27_a_prime,
       not1bit_28_a_prime, not1bit_29_a_prime, not1bit_30_a_prime, not1bit_31_a_prime, not1bit_32_a_prime;
  wire [1:1] and1bit2x1_39_out_2;
  wire [11:3] and1bit2x1_16_out_2;
  wire [15:0] and1bit2x1_6_out_2;
  wire [15:2] and1bit2x1_2_out_2;
  wire [15:7] and1bit2x1_14_out_2;
  wire [15:15] and1bit2x1_30_out_2;

  NOT1bit not1bit_1 (.A(in_1[30]), .A_prime(not1bit_1_a_prime[0]));
  NOT1bit not1bit_2 (.A(in_1[31]), .A_prime(not1bit_1_a_prime[1]));
  AND1bit2x1 and1bit2x1_1 (.in_1(not1bit_1_a_prime), .out_2(not1bit_3_a_prime[1]));
  AND1bit2x1 and1bit2x1_2 (.in_1({not1bit_1_a_prime[1], in_1[30]}), .out_2(and1bit2x1_2_out_2[15]));
  NOT1bit not1bit_3 (.A(in_1[29]), .A_prime(not1bit_3_a_prime[0]));
  AND1bit2x1 and1bit2x1_3 (.in_1(not1bit_3_a_prime), .out_2(not1bit_4_a_prime[1]));
  AND1bit2x1 and1bit2x1_4 (.in_1({not1bit_3_a_prime[1], in_1[29]}), .out_2(and1bit2x1_2_out_2[14]));
  NOT1bit not1bit_4 (.A(in_1[28]), .A_prime(not1bit_4_a_prime[0]));
  AND1bit2x1 and1bit2x1_5 (.in_1(not1bit_4_a_prime), .out_2(not1bit_5_a_prime[1]));
  AND1bit2x1 and1bit2x1_6 (.in_1({not1bit_4_a_prime[1], in_1[28]}), .out_2(and1bit2x1_6_out_2[15]));
  NOT1bit not1bit_5 (.A(in_1[27]), .A_prime(not1bit_5_a_prime[0]));
  AND1bit2x1 and1bit2x1_7 (.in_1(not1bit_5_a_prime), .out_2(not1bit_6_a_prime[1]));
  AND1bit2x1 and1bit2x1_8 (.in_1({not1bit_5_a_prime[1], in_1[27]}), .out_2(and1bit2x1_6_out_2[14]));
  NOT1bit not1bit_6 (.A(in_1[26]), .A_prime(not1bit_6_a_prime[0]));
  AND1bit2x1 and1bit2x1_9 (.in_1(not1bit_6_a_prime), .out_2(not1bit_7_a_prime[1]));
  AND1bit2x1 and1bit2x1_10 (.in_1({not1bit_6_a_prime[1], in_1[26]}), .out_2(and1bit2x1_6_out_2[13]));
  NOT1bit not1bit_7 (.A(in_1[25]), .A_prime(not1bit_7_a_prime[0]));
  AND1bit2x1 and1bit2x1_11 (.in_1(not1bit_7_a_prime), .out_2(not1bit_8_a_prime[1]));
  AND1bit2x1 and1bit2x1_12 (.in_1({not1bit_7_a_prime[1], in_1[25]}), .out_2(and1bit2x1_6_out_2[12]));
  NOT1bit not1bit_8 (.A(in_1[24]), .A_prime(not1bit_8_a_prime[0]));
  AND1bit2x1 and1bit2x1_13 (.in_1(not1bit_8_a_prime), .out_2(not1bit_9_a_prime[1]));
  AND1bit2x1 and1bit2x1_14 (.in_1({not1bit_8_a_prime[1], in_1[24]}), .out_2(and1bit2x1_14_out_2[15]));
  NOT1bit not1bit_9 (.A(in_1[23]), .A_prime(not1bit_9_a_prime[0]));
  AND1bit2x1 and1bit2x1_15 (.in_1(not1bit_9_a_prime), .out_2(not1bit_10_a_prime[1]));
  AND1bit2x1 and1bit2x1_16 (.in_1({not1bit_9_a_prime[1], in_1[23]}), .out_2(and1bit2x1_16_out_2[11]));
  NOT1bit not1bit_10 (.A(in_1[22]), .A_prime(not1bit_10_a_prime[0]));
  AND1bit2x1 and1bit2x1_17 (.in_1(not1bit_10_a_prime), .out_2(not1bit_11_a_prime[1]));
  AND1bit2x1 and1bit2x1_18 (.in_1({not1bit_10_a_prime[1], in_1[22]}), .out_2(and1bit2x1_2_out_2[11]));
  NOT1bit not1bit_11 (.A(in_1[21]), .A_prime(not1bit_11_a_prime[0]));
  AND1bit2x1 and1bit2x1_19 (.in_1(not1bit_11_a_prime), .out_2(not1bit_12_a_prime[1]));
  AND1bit2x1 and1bit2x1_20 (.in_1({not1bit_11_a_prime[1], in_1[21]}), .out_2(and1bit2x1_2_out_2[10]));
  NOT1bit not1bit_12 (.A(in_1[20]), .A_prime(not1bit_12_a_prime[0]));
  AND1bit2x1 and1bit2x1_21 (.in_1(not1bit_12_a_prime), .out_2(not1bit_13_a_prime[1]));
  AND1bit2x1 and1bit2x1_22 (.in_1({not1bit_12_a_prime[1], in_1[20]}), .out_2(and1bit2x1_6_out_2[11]));
  NOT1bit not1bit_13 (.A(in_1[19]), .A_prime(not1bit_13_a_prime[0]));
  AND1bit2x1 and1bit2x1_23 (.in_1(not1bit_13_a_prime), .out_2(not1bit_14_a_prime[1]));
  AND1bit2x1 and1bit2x1_24 (.in_1({not1bit_13_a_prime[1], in_1[19]}), .out_2(and1bit2x1_6_out_2[10]));
  NOT1bit not1bit_14 (.A(in_1[18]), .A_prime(not1bit_14_a_prime[0]));
  AND1bit2x1 and1bit2x1_25 (.in_1(not1bit_14_a_prime), .out_2(not1bit_15_a_prime[1]));
  AND1bit2x1 and1bit2x1_26 (.in_1({not1bit_14_a_prime[1], in_1[18]}), .out_2(and1bit2x1_6_out_2[9]));
  NOT1bit not1bit_15 (.A(in_1[17]), .A_prime(not1bit_15_a_prime[0]));
  AND1bit2x1 and1bit2x1_27 (.in_1(not1bit_15_a_prime), .out_2(not1bit_16_a_prime[1]));
  AND1bit2x1 and1bit2x1_28 (.in_1({not1bit_15_a_prime[1], in_1[17]}), .out_2(and1bit2x1_6_out_2[8]));
  NOT1bit not1bit_16 (.A(in_1[16]), .A_prime(not1bit_16_a_prime[0]));
  AND1bit2x1 and1bit2x1_29 (.in_1(not1bit_16_a_prime), .out_2(not1bit_17_a_prime[1]));
  AND1bit2x1 and1bit2x1_30 (.in_1({not1bit_16_a_prime[1], in_1[16]}), .out_2(and1bit2x1_30_out_2[15]));
  NOT1bit not1bit_17 (.A(in_1[15]), .A_prime(not1bit_17_a_prime[0]));
  AND1bit2x1 and1bit2x1_31 (.in_1(not1bit_17_a_prime), .out_2(not1bit_18_a_prime[1]));
  AND1bit2x1 and1bit2x1_32 (.in_1({not1bit_17_a_prime[1], in_1[15]}), .out_2(and1bit2x1_16_out_2[7]));
  NOT1bit not1bit_18 (.A(in_1[14]), .A_prime(not1bit_18_a_prime[0]));
  AND1bit2x1 and1bit2x1_33 (.in_1(not1bit_18_a_prime), .out_2(not1bit_19_a_prime[1]));
  AND1bit2x1 and1bit2x1_34 (.in_1({not1bit_18_a_prime[1], in_1[14]}), .out_2(and1bit2x1_2_out_2[7]));
  NOT1bit not1bit_19 (.A(in_1[13]), .A_prime(not1bit_19_a_prime[0]));
  AND1bit2x1 and1bit2x1_35 (.in_1(not1bit_19_a_prime), .out_2(not1bit_20_a_prime[1]));
  AND1bit2x1 and1bit2x1_36 (.in_1({not1bit_19_a_prime[1], in_1[13]}), .out_2(and1bit2x1_2_out_2[6]));
  NOT1bit not1bit_20 (.A(in_1[12]), .A_prime(not1bit_20_a_prime[0]));
  AND1bit2x1 and1bit2x1_37 (.in_1(not1bit_20_a_prime), .out_2(not1bit_21_a_prime[1]));
  AND1bit2x1 and1bit2x1_38 (.in_1({not1bit_20_a_prime[1], in_1[12]}), .out_2(and1bit2x1_6_out_2[7]));
  NOT1bit not1bit_21 (.A(in_1[11]), .A_prime(not1bit_21_a_prime[0]));
  AND1bit2x1 and1bit2x1_39 (.in_1(not1bit_21_a_prime), .out_2(and1bit2x1_39_out_2[1]));
  AND1bit2x1 and1bit2x1_40 (.in_1({not1bit_21_a_prime[1], in_1[11]}), .out_2(and1bit2x1_6_out_2[6]));
  NOT1bit not1bit_22 (.A(in_1[10]), .A_prime(not1bit_22_a_prime[0]));
  AND1bit2x1 and1bit2x1_41 (.in_1({and1bit2x1_39_out_2[1], not1bit_22_a_prime[0]}), .out_2(not1bit_23_a_prime[1]));
  AND1bit2x1 and1bit2x1_42 (.in_1({and1bit2x1_39_out_2[1], in_1[10]}), .out_2(and1bit2x1_6_out_2[5]));
  NOT1bit not1bit_23 (.A(in_1[9]), .A_prime(not1bit_23_a_prime[0]));
  AND1bit2x1 and1bit2x1_43 (.in_1(not1bit_23_a_prime), .out_2(not1bit_24_a_prime[1]));
  AND1bit2x1 and1bit2x1_44 (.in_1({not1bit_23_a_prime[1], in_1[9]}), .out_2(and1bit2x1_6_out_2[4]));
  NOT1bit not1bit_24 (.A(in_1[8]), .A_prime(not1bit_24_a_prime[0]));
  AND1bit2x1 and1bit2x1_45 (.in_1(not1bit_24_a_prime), .out_2(not1bit_25_a_prime[1]));
  AND1bit2x1 and1bit2x1_46 (.in_1({not1bit_24_a_prime[1], in_1[8]}), .out_2(and1bit2x1_14_out_2[7]));
  NOT1bit not1bit_25 (.A(in_1[7]), .A_prime(not1bit_25_a_prime[0]));
  AND1bit2x1 and1bit2x1_47 (.in_1(not1bit_25_a_prime), .out_2(not1bit_26_a_prime[1]));
  AND1bit2x1 and1bit2x1_48 (.in_1({not1bit_25_a_prime[1], in_1[7]}), .out_2(and1bit2x1_16_out_2[3]));
  NOT1bit not1bit_26 (.A(in_1[6]), .A_prime(not1bit_26_a_prime[0]));
  AND1bit2x1 and1bit2x1_49 (.in_1(not1bit_26_a_prime), .out_2(not1bit_27_a_prime[1]));
  AND1bit2x1 and1bit2x1_50 (.in_1({not1bit_26_a_prime[1], in_1[6]}), .out_2(and1bit2x1_2_out_2[3]));
  NOT1bit not1bit_27 (.A(in_1[5]), .A_prime(not1bit_27_a_prime[0]));
  AND1bit2x1 and1bit2x1_51 (.in_1(not1bit_27_a_prime), .out_2(not1bit_28_a_prime[1]));
  AND1bit2x1 and1bit2x1_52 (.in_1({not1bit_27_a_prime[1], in_1[5]}), .out_2(and1bit2x1_2_out_2[2]));
  NOT1bit not1bit_28 (.A(in_1[4]), .A_prime(not1bit_28_a_prime[0]));
  AND1bit2x1 and1bit2x1_53 (.in_1(not1bit_28_a_prime), .out_2(not1bit_29_a_prime[1]));
  AND1bit2x1 and1bit2x1_54 (.in_1({not1bit_28_a_prime[1], in_1[4]}), .out_2(and1bit2x1_6_out_2[3]));
  NOT1bit not1bit_29 (.A(in_1[3]), .A_prime(not1bit_29_a_prime[0]));
  AND1bit2x1 and1bit2x1_55 (.in_1(not1bit_29_a_prime), .out_2(not1bit_30_a_prime[1]));
  AND1bit2x1 and1bit2x1_56 (.in_1({not1bit_29_a_prime[1], in_1[3]}), .out_2(and1bit2x1_6_out_2[2]));
  NOT1bit not1bit_30 (.A(in_1[2]), .A_prime(not1bit_30_a_prime[0]));
  AND1bit2x1 and1bit2x1_57 (.in_1(not1bit_30_a_prime), .out_2(not1bit_31_a_prime[1]));
  AND1bit2x1 and1bit2x1_58 (.in_1({not1bit_30_a_prime[1], in_1[2]}), .out_2(and1bit2x1_6_out_2[1]));
  NOT1bit not1bit_31 (.A(in_1[1]), .A_prime(not1bit_31_a_prime[0]));
  AND1bit2x1 and1bit2x1_59 (.in_1(not1bit_31_a_prime), .out_2(not1bit_32_a_prime[1]));
  AND1bit2x1 and1bit2x1_60 (.in_1({not1bit_31_a_prime[1], in_1[1]}), .out_2(and1bit2x1_6_out_2[0]));
  NOT1bit not1bit_32 (.A(in_1[0]), .A_prime(not1bit_32_a_prime[0]));
  AND1bit2x1 and1bit2x1_61 (.in_1(not1bit_32_a_prime), .out_2(and1bit2x1_61_out_2));
  AND1bit2x1 and1bit2x1_62 (.in_1({not1bit_32_a_prime[1], in_1[0]}), .out_2(out_2[5]));
  OR1bit16x1 or1bit16x1_1 (.in_1(and1bit2x1_6_out_2), .out_2(out_2[2]));
  OR1bit16x1 or1bit16x1_2 (
    .in_1({and1bit2x1_2_out_2[15:14], and1bit2x1_6_out_2[13:12], and1bit2x1_2_out_2[11:10], and1bit2x1_6_out_2[9:8], and1bit2x1_2_out_2[7:6], and1bit2x1_6_out_2[5:4], and1bit2x1_2_out_2[3:2], and1bit2x1_6_out_2[1:0]}),
    .out_2(out_2[1]));
  OR1bit16x1 or1bit16x1_3 (
    .in_1({in_1[31], and1bit2x1_2_out_2[14], and1bit2x1_6_out_2[14], and1bit2x1_6_out_2[12], and1bit2x1_16_out_2[11], and1bit2x1_2_out_2[10], and1bit2x1_6_out_2[10], and1bit2x1_6_out_2[8], and1bit2x1_16_out_2[7], and1bit2x1_2_out_2[6], and1bit2x1_6_out_2[6], and1bit2x1_6_out_2[4], and1bit2x1_16_out_2[3], and1bit2x1_2_out_2[2], and1bit2x1_6_out_2[2], and1bit2x1_6_out_2[0]}),
    .out_2(out_2[0]));
  OR1bit16x1 or1bit16x1_4 (
    .in_1({and1bit2x1_14_out_2[15], and1bit2x1_16_out_2[11], and1bit2x1_2_out_2[11:10], and1bit2x1_6_out_2[11:8], and1bit2x1_14_out_2[7], and1bit2x1_16_out_2[3], and1bit2x1_2_out_2[3:2], and1bit2x1_6_out_2[3:0]}),
    .out_2(out_2[3]));
  OR1bit16x1 or1bit16x1_5 (
    .in_1({and1bit2x1_30_out_2[15], and1bit2x1_16_out_2[7], and1bit2x1_2_out_2[7:6], and1bit2x1_6_out_2[7:4], and1bit2x1_14_out_2[7], and1bit2x1_16_out_2[3], and1bit2x1_2_out_2[3:2], and1bit2x1_6_out_2[3:0]}),
    .out_2(out_2[4]));

  assign out_2[11:6] = {6{1'b0}};
endmodule

// Zero
module Zero32bit (
  output [31:0] out_1
);


  assign out_1 = {32{1'b0}};
endmodule

// NOT19
module NOT19bit (
  input  [18:0] Data0,
  output [18:0] DataOut
);

  NOT4bit not4bit_1 (.Data0(Data0[3:0]), .DataOut(DataOut[3:0]));
  NOT4bit not4bit_2 (.Data0(Data0[7:4]), .DataOut(DataOut[7:4]));
  NOT4bit not4bit_3 (.Data0(Data0[11:8]), .DataOut(DataOut[11:8]));
  NOT4bit not4bit_4 (.Data0(Data0[15:12]), .DataOut(DataOut[15:12]));
  NOT3bit not3bit_1 (.Data0(Data0[18:16]), .DataOut(DataOut[18:16]));
endmodule

// M1
module MUX1bit2x1 (
  input  S,
  input  Data0,
  input  Data1,
  output DataOut
);

  wire n74157_1__12__y4, undriven, undriven_2;

  _74157 u_74157_1 (
    ._1__S(S), ._2__A1(Data0), ._3__B1(Data1), ._4__Y1(DataOut), ._8__GND(1'b0), ._16__Vcc(1'b1),
    ._15__G(1'b0), ._14__A4(undriven), ._13__B4(undriven_2), ._12__Y4(n74157_1__12__y4));  // open: _5__A2, _6__B2, _7__Y2, _11__A3, _10__B3, _9__Y3
endmodule

// XOR1
module XOR1bit2x1 (
  input  Data0,
  input  Data1,
  output DataOut
);

  wire n7486_1__11__4y, undriven, undriven_2;

  _7486 u_7486_1 (
    ._1__1A(Data0), ._2__1B(Data1), ._3__1Y(DataOut), ._7__GND(1'b0), ._14__Vcc(1'b1), ._13__4B(undriven),
    ._12__4A(undriven_2), ._11__4Y(n7486_1__11__4y));  // open: _4__2A, _5__2B, _6__2Y, _10__3B, _9__3A, _8__3Y
endmodule
