// Logisim project LightMips.circ as structural Verilog: 17 circuits, main circuit main
module main (
);


  // Notes on the sheet:
  //   CHOBNGMJEFLAIDPK
  //   JMFBDLIGHPOENACK
  //   0 J srl   Logic
  //   1 M sw   Memory
  //   2 F andi   Logic
  //   3 B addi   Arith
  //   4 D subi   Arith
  //   5 L lw   Memory
  //   6 I sll   Logic
  //   7 G or   Logic
  //   8 H ori   Logic
  //   9 P j   Control
  //   10 O bneq   Control
  //   11 E and   Logic
  //   12 N beq   Control
  //   13 A add   Arith
  //   14 C sub   Arith
  //   15 K nor   Logic
endmodule

// insMem0
module InstructionMemory (
  input  [7:0] PC,
  output [7:0] Target_Jump_Address,
  output [3:0] Dst_Reg_Shamt_Addr__Immdt__0_3,
  output [3:0] Src_Reg_2_Dst_Reg__4_7,
  output [3:0] Src_Reg_1__8_11,
  output [3:0] Opcode__12_15
);

  ROM #(.dataWidth(16)) rom_1 (
    .addr(PC), .data({Opcode__12_15, Src_Reg_1__8_11, Src_Reg_2_Dst_Reg__4_7, Dst_Reg_Shamt_Addr__Immdt__0_3}));  // open: sel

  assign Target_Jump_Address = {Src_Reg_1__8_11, Src_Reg_2_Dst_Reg__4_7};

  // Notes on the sheet:
  //   contents of rom_1 (hex, n*v repeats v):
  //   301e 302d 3030 3040 3050 c02a 304f e414 3441 e344 2448 a041 3551 d313 4221 9050 d301 d502 9000
endmodule

// alu0
module ALU4bit (
  input  [2:0] ALUop,
  input  [3:0] A,
  input  [3:0] B,
  output [3:0] Out,
  output Zero
);

  wire or1bit4x1_1_out_2;
  wire [3:0] adder4bit_1_dataout, adder4bit_2_dataout, and_1_out, mux4bit2x1_1_dataout, mux4bit2x1_2_dataout,
       mux4bit2x1_3_dataout, mux4bit2x1_4_dataout, mux4bit2x1_5_dataout, mux4bit2x1_7_dataout,
       n4bitleftshifter_1_out, n4bitrightshifter_1_out, nor_1_out, not4bit_1_dataout, or_1_out;

  Adder4bit adder4bit_1 (.Data0(A), .Data1(B), .Cin(1'b0), .DataOut(adder4bit_1_dataout));  // open: Cout
  NOT4bit not4bit_1 (.Data0(B), .DataOut(not4bit_1_dataout));
  Adder4bit adder4bit_2 (
    .Data0(A), .Data1(not4bit_1_dataout), .Cin(1'b1), .DataOut(adder4bit_2_dataout));  // open: Cout
  assign or_1_out = A | B;  // OR_Gate or_1, 4 bits wide
  assign and_1_out = A & B;  // AND_Gate and_1, 4 bits wide
  assign nor_1_out = ~(A | B);  // NOR_Gate nor_1, 4 bits wide
  _4bitLeftShifter u_4bitleftshifter_1 (.in(A), .shamt(B), .out(n4bitleftshifter_1_out));
  _4bitRightShifter u_4bitrightshifter_1 (.in(A), .shamt(B), .out(n4bitrightshifter_1_out));
  MUX4bit2x1 mux4bit2x1_1 (
    .S(ALUop[0]), .Data0(adder4bit_1_dataout), .Data1(adder4bit_2_dataout), .DataOut(mux4bit2x1_1_dataout));
  MUX4bit2x1 mux4bit2x1_2 (.S(ALUop[0]), .Data0(or_1_out), .Data1(and_1_out), .DataOut(mux4bit2x1_2_dataout));
  MUX4bit2x1 mux4bit2x1_3 (
    .S(ALUop[0]), .Data0(nor_1_out), .Data1(n4bitleftshifter_1_out), .DataOut(mux4bit2x1_3_dataout));
  MUX4bit2x1 mux4bit2x1_4 (
    .S(ALUop[0]), .Data0(n4bitrightshifter_1_out), .Data1(4'b0000), .DataOut(mux4bit2x1_4_dataout));
  MUX4bit2x1 mux4bit2x1_5 (
    .S(ALUop[1]), .Data0(mux4bit2x1_1_dataout), .Data1(mux4bit2x1_2_dataout), .DataOut(mux4bit2x1_5_dataout));
  MUX4bit2x1 mux4bit2x1_6 (.S(ALUop[2]), .Data0(mux4bit2x1_5_dataout), .Data1(mux4bit2x1_7_dataout), .DataOut(Out));
  MUX4bit2x1 mux4bit2x1_7 (
    .S(ALUop[1]), .Data0(mux4bit2x1_3_dataout), .Data1(mux4bit2x1_4_dataout), .DataOut(mux4bit2x1_7_dataout));
  OR1bit4x1 or1bit4x1_1 (.in_1(Out), .out_2(or1bit4x1_1_out_2));
  NOT1bit not1bit_1 (.A(or1bit4x1_1_out_2), .A_prime(Zero));

  // Notes on the sheet:
  //   000 Add
  //   001 Sub
  //   010 And
  //   011 Or
  //   100 Nor
  //   101 SL
  //   110 SR
  //   111 Zero
endmodule

module Control (
  input  [3:0] opCode,
  output jump,
  output RegDst,
  output RegWrite,
  output MemRead,
  output MemWrite,
  output MemtoReg,
  output beq,
  output bneq,
  output ALUsrc,
  output [2:0] ALUop
);

  ROM #(.addrWidth(4), .dataWidth(12)) rom_1 (
    .addr(opCode), .data({ALUop, ALUsrc, bneq, beq, MemtoReg, MemWrite, MemRead, RegWrite, RegDst, jump}),
    .sel(1'b1));

  // Notes on the sheet:
  //   contents of rom_1 (hex, n*v repeats v):
  //   d04 110 704 104 304 12c b04 406 504 1 280 606 240 6 206 806
endmodule

// registers
module Registers (
  input  [3:0] in_zero,
  input  CLKzero,
  input  [3:0] in_t0,
  input  CLK0,
  input  [3:0] in_t1,
  input  CLK1,
  input  [3:0] in_t2,
  input  CLK2,
  input  [3:0] in_t3,
  input  CLK3,
  input  [3:0] in_t4,
  input  CLK4,
  input  [3:0] in_sp,
  input  CLKsp,
  output [3:0] zero,
  output [3:0] t0,
  output [3:0] t1,
  output [3:0] t2,
  output [3:0] t3,
  output [3:0] t4,
  output [3:0] sp
);

  wire [3:0] n7474_1__5__q1;

  _7474 u_7474_1 (
    ._2__D1(in_zero[0]), ._3__CLK1(CLKzero), ._5__Q1(n7474_1__5__q1[0]), ._7__GND(1'b0), ._14__Vcc(1'b1),
    ._12__D2(in_zero[1]), ._11__CLK2(CLKzero), ._9__Q2(n7474_1__5__q1[1]));  // open: _1__CLR1, _4__PR1, _6__nQ1, _13__CLR2, _10__PR2, _8__nQ2
  _7474 u_7474_2 (
    ._2__D1(in_zero[2]), ._3__CLK1(CLKzero), ._5__Q1(n7474_1__5__q1[2]), ._7__GND(1'b0), ._14__Vcc(1'b1),
    ._12__D2(in_zero[3]), ._11__CLK2(CLKzero), ._9__Q2(n7474_1__5__q1[3]));  // open: _1__CLR1, _4__PR1, _6__nQ1, _13__CLR2, _10__PR2, _8__nQ2
  _7474 u_7474_3 (
    ._2__D1(in_t0[0]), ._3__CLK1(CLK0), ._5__Q1(t0[0]), ._7__GND(1'b0), ._14__Vcc(1'b1), ._12__D2(in_t0[1]),
    ._11__CLK2(CLK0), ._9__Q2(t0[1]));  // open: _1__CLR1, _4__PR1, _6__nQ1, _13__CLR2, _10__PR2, _8__nQ2
  _7474 u_7474_4 (
    ._2__D1(in_t0[2]), ._3__CLK1(CLK0), ._5__Q1(t0[2]), ._7__GND(1'b0), ._14__Vcc(1'b1), ._12__D2(in_t0[3]),
    ._11__CLK2(CLK0), ._9__Q2(t0[3]));  // open: _1__CLR1, _4__PR1, _6__nQ1, _13__CLR2, _10__PR2, _8__nQ2
  _7474 u_7474_5 (
    ._2__D1(in_t1[0]), ._3__CLK1(CLK1), ._5__Q1(t1[0]), ._7__GND(1'b0), ._14__Vcc(1'b1), ._12__D2(in_t1[1]),
    ._11__CLK2(CLK1), ._9__Q2(t1[1]));  // open: _1__CLR1, _4__PR1, _6__nQ1, _13__CLR2, _10__PR2, _8__nQ2
  _7474 u_7474_6 (
    ._2__D1(in_t1[2]), ._3__CLK1(CLK1), ._5__Q1(t1[2]), ._7__GND(1'b0), ._14__Vcc(1'b1), ._12__D2(in_t1[3]),
    ._11__CLK2(CLK1), ._9__Q2(t1[3]));  // open: _1__CLR1, _4__PR1, _6__nQ1, _13__CLR2, _10__PR2, _8__nQ2
  _7474 u_7474_7 (
    ._2__D1(in_t2[0]), ._3__CLK1(CLK2), ._5__Q1(t2[0]), ._7__GND(1'b0), ._14__Vcc(1'b1), ._12__D2(in_t2[1]),
    ._11__CLK2(CLK2), ._9__Q2(t2[1]));  // open: _1__CLR1, _4__PR1, _6__nQ1, _13__CLR2, _10__PR2, _8__nQ2
  _7474 u_7474_8 (
    ._2__D1(in_t2[2]), ._3__CLK1(CLK2), ._5__Q1(t2[2]), ._7__GND(1'b0), ._14__Vcc(1'b1), ._12__D2(in_t2[3]),
    ._11__CLK2(CLK2), ._9__Q2(t2[3]));  // open: _1__CLR1, _4__PR1, _6__nQ1, _13__CLR2, _10__PR2, _8__nQ2
  _7474 u_7474_9 (
    ._2__D1(in_t3[0]), ._3__CLK1(CLK3), ._5__Q1(t3[0]), ._7__GND(1'b0), ._14__Vcc(1'b1), ._12__D2(in_t3[1]),
    ._11__CLK2(CLK3), ._9__Q2(t3[1]));  // open: _1__CLR1, _4__PR1, _6__nQ1, _13__CLR2, _10__PR2, _8__nQ2
  _7474 u_7474_10 (
    ._2__D1(in_t3[2]), ._3__CLK1(CLK3), ._5__Q1(t3[2]), ._7__GND(1'b0), ._14__Vcc(1'b1), ._12__D2(in_t3[3]),
    ._11__CLK2(CLK3), ._9__Q2(t3[3]));  // open: _1__CLR1, _4__PR1, _6__nQ1, _13__CLR2, _10__PR2, _8__nQ2
  _7474 u_7474_11 (
    ._2__D1(in_t4[0]), ._3__CLK1(CLK4), ._5__Q1(t4[0]), ._7__GND(1'b0), ._14__Vcc(1'b1), ._12__D2(in_t4[1]),
    ._11__CLK2(CLK4), ._9__Q2(t4[1]));  // open: _1__CLR1, _4__PR1, _6__nQ1, _13__CLR2, _10__PR2, _8__nQ2
  _7474 u_7474_12 (
    ._2__D1(in_t4[2]), ._3__CLK1(CLK4), ._5__Q1(t4[2]), ._7__GND(1'b0), ._14__Vcc(1'b1), ._12__D2(in_t4[3]),
    ._11__CLK2(CLK4), ._9__Q2(t4[3]));  // open: _1__CLR1, _4__PR1, _6__nQ1, _13__CLR2, _10__PR2, _8__nQ2
  _7474 u_7474_13 (
    ._2__D1(in_sp[0]), ._3__CLK1(CLKsp), ._5__Q1(sp[0]), ._7__GND(1'b0), ._14__Vcc(1'b1), ._12__D2(in_sp[1]),
    ._11__CLK2(CLKsp), ._9__Q2(sp[1]));  // open: _1__CLR1, _4__PR1, _6__nQ1, _13__CLR2, _10__PR2, _8__nQ2
  _7474 u_7474_14 (
    ._2__D1(in_sp[2]), ._3__CLK1(CLKsp), ._5__Q1(sp[2]), ._7__GND(1'b0), ._14__Vcc(1'b1), ._12__D2(in_sp[3]),
    ._11__CLK2(CLKsp), ._9__Q2(sp[3]));  // open: _1__CLR1, _4__PR1, _6__nQ1, _13__CLR2, _10__PR2, _8__nQ2

  assign zero = 4'b0000;
endmodule

// regFile0
module RegisterFile (
  input  [3:0] Reg_1_Address,
  input  [3:0] Reg_2_Address,
  input  [3:0] Write_Data,
  input  [3:0] Write_Reg_Address,
  input  RegWrite,
  input  Clk,
  output [3:0] Read_Data_1,
  output [3:0] Read_Data_2,
  output [3:0] zero,
  output [3:0] t0,
  output [3:0] t1,
  output [3:0] t2,
  output [3:0] t3,
  output [3:0] t4,
  output [3:0] sp
);

  wire and_1_out, decoder_1_out1, decoder_1_out2, decoder_1_out3, decoder_1_out4, decoder_1_out5,
       decoder_1_out6;
  wire [2:0] multiplexer_1_out;

  Multiplexer #(.width(3), .enable("false")) multiplexer_1 (
    .in0(3'b000), .in1(Write_Reg_Address[2:0]), .out(multiplexer_1_out), .sel(and_1_out));
  and and_1 (and_1_out, RegWrite, Clk);
  Decoder #(.select(3), .enable("false")) decoder_1 (
    .out1(decoder_1_out1), .out2(decoder_1_out2), .out3(decoder_1_out3), .out4(decoder_1_out4),
    .out5(decoder_1_out5), .out6(decoder_1_out6), .sel(multiplexer_1_out));  // open: out0, out7
  Registers registers_1 (
    .in_t0(Write_Data), .CLK0(decoder_1_out1), .in_t1(Write_Data), .CLK1(decoder_1_out2), .in_t2(Write_Data),
    .CLK2(decoder_1_out3), .in_t3(Write_Data), .CLK3(decoder_1_out4), .in_t4(Write_Data),
    .CLK4(decoder_1_out5), .in_sp(Write_Data), .CLKsp(decoder_1_out6), .zero(zero), .t0(t0), .t1(t1),
    .t2(t2), .t3(t3), .t4(t4), .sp(sp));  // open: in_zero, CLKzero
  Multiplexer #(.select(3), .width(4), .enable("false")) multiplexer_2 (
    .in0(zero), .in1(t0), .in2(t1), .in3(t2), .in4(t3), .in5(t4), .in6(sp), .out(Read_Data_1),
    .sel(Reg_1_Address[2:0]));  // open: in7
  Multiplexer #(.select(3), .width(4), .enable("false")) multiplexer_3 (
    .in0(zero), .in1(t0), .in2(t1), .in3(t2), .in4(t3), .in5(t4), .in6(sp), .out(Read_Data_2),
    .sel(Reg_2_Address[2:0]));  // open: in7
endmodule

// dataMem0
module DataMemory (
  input  [3:0] Address,
  input  [3:0] Write_Data,
  input  MemWrite,
  input  MemRead,
  input  CLK,
  output [3:0] MemData
);

  RAM #(.addrWidth(4), .dataWidth(4), .bus("separate")) ram_1 (
    .addr(Address), .din(Write_Data), .data(MemData), .str(MemWrite), .clk(CLK), .ld(MemRead));  // open: sel, clr
endmodule

// 8bitReg
module Reg8bit (
  input  [7:0] in,
  input  CLK0,
  output [7:0] out
);

  _7474 u_7474_1 (
    ._2__D1(in[0]), ._3__CLK1(CLK0), ._5__Q1(out[0]), ._7__GND(1'b0), ._14__Vcc(1'b1), ._12__D2(in[1]),
    ._11__CLK2(CLK0), ._9__Q2(out[1]));  // open: _1__CLR1, _4__PR1, _6__nQ1, _13__CLR2, _10__PR2, _8__nQ2
  _7474 u_7474_2 (
    ._2__D1(in[2]), ._3__CLK1(CLK0), ._5__Q1(out[2]), ._7__GND(1'b0), ._14__Vcc(1'b1), ._12__D2(in[3]),
    ._11__CLK2(CLK0), ._9__Q2(out[3]));  // open: _1__CLR1, _4__PR1, _6__nQ1, _13__CLR2, _10__PR2, _8__nQ2
  _7474 u_7474_3 (
    ._2__D1(in[4]), ._3__CLK1(CLK0), ._5__Q1(out[4]), ._7__GND(1'b0), ._14__Vcc(1'b1), ._12__D2(in[5]),
    ._11__CLK2(CLK0), ._9__Q2(out[5]));  // open: _1__CLR1, _4__PR1, _6__nQ1, _13__CLR2, _10__PR2, _8__nQ2
  _7474 u_7474_4 (
    ._2__D1(in[6]), ._3__CLK1(CLK0), ._5__Q1(out[6]), ._7__GND(1'b0), ._14__Vcc(1'b1), ._12__D2(in[7]),
    ._11__CLK2(CLK0), ._9__Q2(out[7]));  // open: _1__CLR1, _4__PR1, _6__nQ1, _13__CLR2, _10__PR2, _8__nQ2
endmodule

// bALU
module BranchAlu (
  input  [7:0] insIN,
  input  [3:0] brel,
  output [7:0] insOUT
);

  wire [7:0] adder_1_out, negator_1_out, subtractor_1_out;

  Negator negator_1 (.in({{5{brel[3]}}, brel[2:0]}), .out(negator_1_out));
  Adder adder_1 (.a(insIN), .b({{5{brel[3]}}, brel[2:0]}), .out(adder_1_out));  // open: cin, cout
  Subtractor subtractor_1 (.a(insIN), .b(negator_1_out), .out(subtractor_1_out));  // open: bin, bout
  Multiplexer #(.width(8), .enable("false")) multiplexer_1 (
    .in0(adder_1_out), .in1(subtractor_1_out), .out(insOUT), .sel(brel[3]));
endmodule

// DataMemory
module dataMemEn1 (
  input  MemToReg,
  input  [3:0] Address,
  input  [3:0] WriteData,
  input  MemWrite,
  input  MemRead,
  input  CLK,
  output [3:0] WriteBack
);

  wire [3:0] datamemory_1_memdata;

  DataMemory datamemory_1 (
    .Address(Address), .Write_Data(WriteData), .MemWrite(MemWrite), .MemRead(MemRead), .CLK(CLK),
    .MemData(datamemory_1_memdata));
  Multiplexer #(.width(4), .enable("false")) multiplexer_1 (
    .in0(Address), .in1(datamemory_1_memdata), .out(WriteBack), .sel(MemToReg));
endmodule

// ALU
module aluEn1 (
  input  beq,
  input  bneq,
  input  ALUsrc,
  input  [2:0] ALUop,
  input  [3:0] Read_Data_1,
  input  [3:0] Read_Data_2,
  input  [3:0] Dst_Reg_Shamt_Addr__Immdt__0_3,
  output bsel,
  output [3:0] out
);

  wire alu4bit_1_zero, n7408_1__3__1y, n7408_1__6__2y, not_1_out;
  wire [3:0] multiplexer_1_out;

  Multiplexer #(.width(4), .enable("false")) multiplexer_1 (
    .in0(Read_Data_2), .in1(Dst_Reg_Shamt_Addr__Immdt__0_3), .out(multiplexer_1_out), .sel(ALUsrc));
  not not_1 (not_1_out, alu4bit_1_zero);
  ALU4bit alu4bit_1 (.ALUop(ALUop), .A(Read_Data_1), .B(multiplexer_1_out), .Out(out), .Zero(alu4bit_1_zero));
  or or_1 (bsel, n7408_1__3__1y, n7408_1__6__2y);
  _7408 u_7408_1 (
    ._1__1A(beq), ._2__1B(alu4bit_1_zero), ._3__1Y(n7408_1__3__1y), ._4__2A(bneq), ._5__2B(not_1_out),
    ._6__2Y(n7408_1__6__2y));  // open: _7__GND, _14__Vcc, _13__4B, _12__4A, _11__4Y, _10__3B, _9__3A, _8__3Y
endmodule

// RegisterFile
module regFileEn1 (
  input  RegDst,
  input  RegWrite,
  input  [3:0] Dst_Reg_Shamt_Addr__Immdt__0_3,
  input  [3:0] Src_Reg_2_Dst_Reg__4_7,
  input  [3:0] Src_Reg_1__8_11,
  input  [3:0] Write_Data,
  input  CLK,
  output [3:0] Read_Data_1,
  output [3:0] Read_Data_2,
  output [3:0] zero,
  output [3:0] t0,
  output [3:0] t1,
  output [3:0] t2,
  output [3:0] t3,
  output [3:0] t4,
  output [3:0] sp
);

  wire [3:0] multiplexer_1_out;

  Multiplexer #(.width(4), .enable("false")) multiplexer_1 (
    .in0(Src_Reg_2_Dst_Reg__4_7), .in1(Dst_Reg_Shamt_Addr__Immdt__0_3), .out(multiplexer_1_out), .sel(RegDst));
  RegisterFile registerfile_1 (
    .Reg_1_Address(Src_Reg_1__8_11), .Reg_2_Address(Src_Reg_2_Dst_Reg__4_7), .Write_Data(Write_Data),
    .Write_Reg_Address(multiplexer_1_out), .RegWrite(RegWrite), .Clk(CLK), .Read_Data_1(Read_Data_1),
    .Read_Data_2(Read_Data_2), .zero(zero), .t0(t0), .t1(t1), .t2(t2), .t3(t3), .t4(t4), .sp(sp));
endmodule

// Instruction
module insMemEn1 (
  input  Jump,
  input  bsel,
  input  CLK,
  output [7:0] PC,
  output [3:0] Dst_Reg_Shamt_Addr__Immdt__0_3,
  output [3:0] Src_Reg_2_Dst_Reg__4_7,
  output [3:0] Src_Reg_1__8_11,
  output [3:0] Opcode__12_15
);

  wire n7474_1__5__q1, not_1_out;
  wire [7:0] adder_1_out, branchalu_1_insout, instructionmemory_1_target_jump_address, multiplexer_2_out,
       multiplexer_3_out, reg8bit_1_out;

  Reg8bit reg8bit_1 (.in(multiplexer_3_out), .CLK0(not_1_out), .out(reg8bit_1_out));
  not not_1 (not_1_out, CLK);
  Multiplexer #(.width(8), .enable("false")) multiplexer_1 (
    .in0({8{1'b0}}), .in1(reg8bit_1_out), .out(PC), .sel(n7474_1__5__q1));
  _7474 u_7474_1 (
    ._2__D1(1'b1), ._3__CLK1(CLK), ._5__Q1(n7474_1__5__q1), ._7__GND(1'b0), ._14__Vcc(1'b1));  // open: _1__CLR1, _4__PR1, _6__nQ1, _13__CLR2, _12__D2, _11__CLK2, _10__PR2, _9__Q2, _8__nQ2
  InstructionMemory instructionmemory_1 (
    .PC(PC), .Target_Jump_Address(instructionmemory_1_target_jump_address),
    .Dst_Reg_Shamt_Addr__Immdt__0_3(Dst_Reg_Shamt_Addr__Immdt__0_3),
    .Src_Reg_2_Dst_Reg__4_7(Src_Reg_2_Dst_Reg__4_7), .Src_Reg_1__8_11(Src_Reg_1__8_11),
    .Opcode__12_15(Opcode__12_15));
  Adder adder_1 (.a(PC), .b({8{1'b0}}), .out(adder_1_out), .cin(1'b1));  // open: cout
  BranchAlu branchalu_1 (.insIN(adder_1_out), .brel(Dst_Reg_Shamt_Addr__Immdt__0_3), .insOUT(branchalu_1_insout));
  Multiplexer #(.width(8), .enable("false")) multiplexer_2 (
    .in0(adder_1_out), .in1(branchalu_1_insout), .out(multiplexer_2_out), .sel(bsel));
  Multiplexer #(.width(8), .enable("false")) multiplexer_3 (
    .in0(multiplexer_2_out), .in1(instructionmemory_1_target_jump_address), .out(multiplexer_3_out),
    .sel(Jump));

  // Notes on the sheet:
  //   PC
endmodule

module mips (
  input  clk,
  output [3:0] zero,
  output [3:0] zero_2,
  output [3:0] zero_3,
  output [3:0] zero_4,
  output [3:0] zero_5,
  output [3:0] zero_6,
  output [3:0] zero_7,
  output [3:0] zero_8,
  output [3:0] zero_9,
  output [3:0] zero_10,
  output [3:0] zero_11,
  output [3:0] zero_12,
  output [3:0] zero_13,
  output [3:0] t0,
  output [7:0] pc,
  output [3:0] t1,
  output [3:0] zero_14,
  output [3:0] t2,
  output [3:0] t3,
  output [3:0] t4,
  output [3:0] sp
);

  wire aluen1_1_bsel, control_1_alusrc, control_1_beq, control_1_bneq, control_1_jump, control_1_memread,
       control_1_memtoreg, control_1_memwrite, control_1_regdst, control_1_regwrite;
  wire [2:0] control_1_aluop;
  wire [3:0] aluen1_1_out;

  insMemEn1 insmemen1_1 (
    .Jump(control_1_jump), .bsel(aluen1_1_bsel), .CLK(clk), .Dst_Reg_Shamt_Addr__Immdt__0_3(zero_2),
    .Src_Reg_2_Dst_Reg__4_7(zero_5), .Src_Reg_1__8_11(zero_3), .Opcode__12_15(zero_11), .PC(pc));
  Control control_1 (
    .opCode(zero_11), .jump(control_1_jump), .RegDst(control_1_regdst), .RegWrite(control_1_regwrite),
    .MemRead(control_1_memread), .MemWrite(control_1_memwrite), .MemtoReg(control_1_memtoreg),
    .beq(control_1_beq), .bneq(control_1_bneq), .ALUsrc(control_1_alusrc), .ALUop(control_1_aluop));
  regFileEn1 regfileen1_1 (
    .RegDst(control_1_regdst), .RegWrite(control_1_regwrite), .Dst_Reg_Shamt_Addr__Immdt__0_3(zero_2),
    .Src_Reg_2_Dst_Reg__4_7(zero_5), .Src_Reg_1__8_11(zero_3), .Write_Data(zero), .CLK(clk),
    .Read_Data_1(zero_10), .Read_Data_2(zero_7), .zero(zero_13), .t0(t0), .t1(t1), .t2(t2), .t3(t3), .t4(t4),
    .sp(sp));
  aluEn1 aluen1_1 (
    .beq(control_1_beq), .bneq(control_1_bneq), .ALUsrc(control_1_alusrc), .ALUop(control_1_aluop),
    .Read_Data_1(zero_10), .Read_Data_2(zero_7), .Dst_Reg_Shamt_Addr__Immdt__0_3(zero_2),
    .bsel(aluen1_1_bsel), .out(aluen1_1_out));
  dataMemEn1 datamemen1_1 (
    .MemToReg(control_1_memtoreg), .Address(aluen1_1_out), .WriteData(zero_7), .MemWrite(control_1_memwrite),
    .MemRead(control_1_memread), .CLK(clk), .WriteBack(zero));

  assign zero_6 = zero_5;
  assign zero_8 = zero_3;
  assign zero_9 = zero_2;
  assign zero_12 = zero_2;
  assign zero_14 = zero;
endmodule

module propermips (
  input  clk,
  output [7:0] pc,
  output [3:0] t0,
  output [3:0] t0_2,
  output [3:0] t1,
  output [3:0] t2,
  output [3:0] t3,
  output [3:0] t4
);

  wire adder4bit_1_cout, aluen2_1_bsel, control_1_alusrc, control_1_beq, control_1_bneq, control_1_jump,
       control_1_memread, control_1_memtoreg, control_1_memwrite, control_1_regdst, control_1_regwrite,
       not1bit_1_a_prime;
  wire [2:0] control_1_aluop, instructionmemory_1_dst_reg_shamt_addr__immdt__0_3_2;
  wire [3:0] adder4bit_1_dataout, adder4bit_2_dataout, datamemory_1_memdata,
       instructionmemory_1_opcode__12_15, instructionmemory_1_src_reg_1__8_11,
       instructionmemory_1_src_reg_2_dst_reg__4_7, mux4bit2x1_1_dataout, mux4bit2x1_2_dataout,
       mux4bit2x1_3_dataout, mux4bit2x1_4_dataout, mux4bit2x1_5_dataout, mux4bit2x1_6_dataout,
       mux4bit2x1_7_dataout, registerfile_1_read_data_1, registerfile_1_read_data_2;
  wire [3:3] instructionmemory_1_dst_reg_shamt_addr__immdt__0_3;

  InstructionMemory instructionmemory_1 (
    .PC(pc),
    .Dst_Reg_Shamt_Addr__Immdt__0_3({instructionmemory_1_dst_reg_shamt_addr__immdt__0_3[3], instructionmemory_1_dst_reg_shamt_addr__immdt__0_3_2}),
    .Src_Reg_2_Dst_Reg__4_7(instructionmemory_1_src_reg_2_dst_reg__4_7),
    .Src_Reg_1__8_11(instructionmemory_1_src_reg_1__8_11), .Opcode__12_15(instructionmemory_1_opcode__12_15));  // open: Target_Jump_Address
  Reg8bit reg8bit_1 (.in({mux4bit2x1_4_dataout, mux4bit2x1_3_dataout}), .CLK0(not1bit_1_a_prime), .out(pc));
  NOT1bit not1bit_1 (.A(clk), .A_prime(not1bit_1_a_prime));
  MUX4bit2x1 mux4bit2x1_1 (
    .S(aluen2_1_bsel), .Data0(4'b0000),
    .Data1({instructionmemory_1_dst_reg_shamt_addr__immdt__0_3[3], instructionmemory_1_dst_reg_shamt_addr__immdt__0_3_2}),
    .DataOut(mux4bit2x1_1_dataout));
  MUX4bit2x1 mux4bit2x1_2 (
    .S(aluen2_1_bsel), .Data0(4'b0000), .Data1({4{instructionmemory_1_dst_reg_shamt_addr__immdt__0_3[3]}}),
    .DataOut(mux4bit2x1_2_dataout));
  Adder4bit adder4bit_1 (
    .Data0(pc[3:0]), .Data1(mux4bit2x1_1_dataout), .Cin(1'b1), .Cout(adder4bit_1_cout),
    .DataOut(adder4bit_1_dataout));
  Adder4bit adder4bit_2 (
    .Data0(pc[7:4]), .Data1(mux4bit2x1_2_dataout), .Cin(adder4bit_1_cout), .DataOut(adder4bit_2_dataout));  // open: Cout
  MUX4bit2x1 mux4bit2x1_3 (
    .S(control_1_jump), .Data0(adder4bit_1_dataout), .Data1(instructionmemory_1_src_reg_2_dst_reg__4_7),
    .DataOut(mux4bit2x1_3_dataout));
  MUX4bit2x1 mux4bit2x1_4 (
    .S(control_1_jump), .Data0(adder4bit_2_dataout), .Data1(instructionmemory_1_src_reg_1__8_11),
    .DataOut(mux4bit2x1_4_dataout));
  Control control_1 (
    .opCode(instructionmemory_1_opcode__12_15), .jump(control_1_jump), .RegDst(control_1_regdst),
    .RegWrite(control_1_regwrite), .MemRead(control_1_memread), .MemWrite(control_1_memwrite),
    .MemtoReg(control_1_memtoreg), .beq(control_1_beq), .bneq(control_1_bneq), .ALUsrc(control_1_alusrc),
    .ALUop(control_1_aluop));
  MUX4bit2x1 mux4bit2x1_5 (
    .S(control_1_regdst), .Data0(instructionmemory_1_src_reg_2_dst_reg__4_7),
    .Data1({instructionmemory_1_dst_reg_shamt_addr__immdt__0_3[3], instructionmemory_1_dst_reg_shamt_addr__immdt__0_3_2}),
    .DataOut(mux4bit2x1_5_dataout));
  RegisterFile registerfile_1 (
    .Reg_1_Address(instructionmemory_1_src_reg_1__8_11),
    .Reg_2_Address(instructionmemory_1_src_reg_2_dst_reg__4_7), .Write_Data(mux4bit2x1_7_dataout),
    .Write_Reg_Address(mux4bit2x1_5_dataout), .RegWrite(control_1_regwrite), .Clk(clk),
    .Read_Data_1(registerfile_1_read_data_1), .Read_Data_2(registerfile_1_read_data_2), .t0(t0_2), .t1(t1),
    .t2(t2), .t3(t3), .t4(t4));  // open: zero, sp
  MUX4bit2x1 mux4bit2x1_6 (
    .S(control_1_alusrc), .Data0(registerfile_1_read_data_2),
    .Data1({instructionmemory_1_dst_reg_shamt_addr__immdt__0_3[3], instructionmemory_1_dst_reg_shamt_addr__immdt__0_3_2}),
    .DataOut(mux4bit2x1_6_dataout));
  aluEn2 aluen2_1 (
    .beq(control_1_beq), .bneq(control_1_bneq), .ALUop(control_1_aluop),
    .Read_Data_1(registerfile_1_read_data_1), .Read_Data_2(mux4bit2x1_6_dataout), .bsel(aluen2_1_bsel),
    .out(t0));
  DataMemory datamemory_1 (
    .Address(t0), .Write_Data(registerfile_1_read_data_2), .MemWrite(control_1_memwrite),
    .MemRead(control_1_memread), .CLK(clk), .MemData(datamemory_1_memdata));
  MUX4bit2x1 mux4bit2x1_7 (
    .S(control_1_memtoreg), .Data0(t0), .Data1(datamemory_1_memdata), .DataOut(mux4bit2x1_7_dataout));
endmodule

// alu2
module aluEn2 (
  input  beq,
  input  bneq,
  input  [2:0] ALUop,
  input  [3:0] Read_Data_1,
  input  [3:0] Read_Data_2,
  output bsel,
  output [3:0] out
);

  wire alu4bit_1_zero, n7408_1__3__1y, n7408_1__6__2y, not_1_out;

  not not_1 (not_1_out, alu4bit_1_zero);
  ALU4bit alu4bit_1 (.ALUop(ALUop), .A(Read_Data_1), .B(Read_Data_2), .Out(out), .Zero(alu4bit_1_zero));
  or or_1 (bsel, n7408_1__3__1y, n7408_1__6__2y);
  _7408 u_7408_1 (
    ._1__1A(beq), ._2__1B(alu4bit_1_zero), ._3__1Y(n7408_1__3__1y), ._4__2A(bneq), ._5__2B(not_1_out),
    ._6__2Y(n7408_1__6__2y));  // open: _7__GND, _14__Vcc, _13__4B, _12__4A, _11__4Y, _10__3B, _9__3A, _8__3Y
endmodule

module hwlog (
  input  clk,
  output [7:0] pc,
  output [3:0] t0,
  output [3:0] t1,
  output [3:0] t2,
  output [3:0] t3,
  output [3:0] t4
);

  wire adder4bit_1_cout, aluen2_1_bsel, control_1_alusrc, control_1_beq, control_1_bneq, control_1_jump,
       control_1_memread, control_1_memtoreg, control_1_memwrite, control_1_regdst, control_1_regwrite,
       not1bit_1_a_prime;
  wire [2:0] control_1_aluop;
  wire [3:0] adder4bit_1_dataout, adder4bit_2_dataout, aluen2_1_out, datamemory_1_memdata,
       instructionmemory_1_dst_reg_shamt_addr__immdt__0_3, instructionmemory_1_opcode__12_15,
       instructionmemory_1_src_reg_1__8_11, instructionmemory_1_src_reg_2_dst_reg__4_7, mux4bit2x1_1_dataout,
       mux4bit2x1_2_dataout, mux4bit2x1_3_dataout, mux4bit2x1_4_dataout, mux4bit2x1_5_dataout,
       mux4bit2x1_6_dataout, registerfile_1_read_data_1, registerfile_1_read_data_2;

  InstructionMemory instructionmemory_1 (
    .PC(pc), .Dst_Reg_Shamt_Addr__Immdt__0_3(instructionmemory_1_dst_reg_shamt_addr__immdt__0_3),
    .Src_Reg_2_Dst_Reg__4_7(instructionmemory_1_src_reg_2_dst_reg__4_7),
    .Src_Reg_1__8_11(instructionmemory_1_src_reg_1__8_11), .Opcode__12_15(instructionmemory_1_opcode__12_15));  // open: Target_Jump_Address
  Reg8bit reg8bit_1 (.in({mux4bit2x1_3_dataout, mux4bit2x1_2_dataout}), .CLK0(not1bit_1_a_prime), .out(pc));
  NOT1bit not1bit_1 (.A(clk), .A_prime(not1bit_1_a_prime));
  MUX4bit2x1 mux4bit2x1_1 (
    .S(aluen2_1_bsel), .Data0(4'b0000), .Data1(instructionmemory_1_dst_reg_shamt_addr__immdt__0_3),
    .DataOut(mux4bit2x1_1_dataout));
  Adder4bit adder4bit_1 (
    .Data0(pc[3:0]), .Data1(mux4bit2x1_1_dataout), .Cin(1'b1), .Cout(adder4bit_1_cout),
    .DataOut(adder4bit_1_dataout));
  Adder4bit adder4bit_2 (
    .Data0(pc[7:4]), .Data1(4'b0000), .Cin(adder4bit_1_cout), .DataOut(adder4bit_2_dataout));  // open: Cout
  MUX4bit2x1 mux4bit2x1_2 (
    .S(control_1_jump), .Data0(adder4bit_1_dataout), .Data1(instructionmemory_1_src_reg_2_dst_reg__4_7),
    .DataOut(mux4bit2x1_2_dataout));
  MUX4bit2x1 mux4bit2x1_3 (
    .S(control_1_jump), .Data0(adder4bit_2_dataout), .Data1(instructionmemory_1_src_reg_1__8_11),
    .DataOut(mux4bit2x1_3_dataout));
  Control control_1 (
    .opCode(instructionmemory_1_opcode__12_15), .jump(control_1_jump), .RegDst(control_1_regdst),
    .RegWrite(control_1_regwrite), .MemRead(control_1_memread), .MemWrite(control_1_memwrite),
    .MemtoReg(control_1_memtoreg), .beq(control_1_beq), .bneq(control_1_bneq), .ALUsrc(control_1_alusrc),
    .ALUop(control_1_aluop));
  MUX4bit2x1 mux4bit2x1_4 (
    .S(control_1_regdst), .Data0(instructionmemory_1_src_reg_2_dst_reg__4_7),
    .Data1(instructionmemory_1_dst_reg_shamt_addr__immdt__0_3), .DataOut(mux4bit2x1_4_dataout));
  RegisterFile registerfile_1 (
    .Reg_1_Address(instructionmemory_1_src_reg_1__8_11),
    .Reg_2_Address(instructionmemory_1_src_reg_2_dst_reg__4_7), .Write_Data(mux4bit2x1_6_dataout),
    .Write_Reg_Address(mux4bit2x1_4_dataout), .RegWrite(control_1_regwrite), .Clk(clk),
    .Read_Data_1(registerfile_1_read_data_1), .Read_Data_2(registerfile_1_read_data_2), .t0(t0), .t1(t1),
    .t2(t2), .t3(t3), .t4(t4));  // open: zero, sp
  MUX4bit2x1 mux4bit2x1_5 (
    .S(control_1_alusrc), .Data0(registerfile_1_read_data_2),
    .Data1(instructionmemory_1_dst_reg_shamt_addr__immdt__0_3), .DataOut(mux4bit2x1_5_dataout));
  aluEn2 aluen2_1 (
    .beq(control_1_beq), .bneq(control_1_bneq), .ALUop(control_1_aluop),
    .Read_Data_1(registerfile_1_read_data_1), .Read_Data_2(mux4bit2x1_5_dataout), .bsel(aluen2_1_bsel),
    .out(aluen2_1_out));
  DataMemory datamemory_1 (
    .Address(aluen2_1_out), .Write_Data(registerfile_1_read_data_2), .MemWrite(control_1_memwrite),
    .MemRead(control_1_memread), .CLK(clk), .MemData(datamemory_1_memdata));
  MUX4bit2x1 mux4bit2x1_6 (
    .S(control_1_memtoreg), .Data0(aluen2_1_out), .Data1(datamemory_1_memdata), .DataOut(mux4bit2x1_6_dataout));
endmodule
